// Logisim project 4-1-MUX-Tunnel.circ as structural Verilog: 1 circuit, main circuit main
module main (
  input  [3:0] INPUT,
  input  [1:0] SELECT,
  output OUTPUT
);

  wire main_1_y, main_2_y;

  _2_1MUX_main main_1 (.D0(INPUT[0]), .D1(SELECT[0]), .S(INPUT[1]), .Y(main_1_y));
  _2_1MUX_main main_2 (.D0(INPUT[2]), .D1(SELECT[0]), .S(INPUT[3]), .Y(main_2_y));
  _2_1MUX_main main_3 (.D0(main_1_y), .D1(SELECT[1]), .S(main_2_y), .Y(OUTPUT));

  // Other names for the same wires on the sheet: DATA[3:0] = INPUT; S[1:0] = SELECT; Y = OUTPUT
endmodule
