// Logisim project 4-1MUX.circ as structural Verilog: 1 circuit, main circuit main
module main (
  input  D0,
  input  D1,
  input  D2,
  input  D3,
  input  S0,
  input  S1,
  output Y
);

  wire main_1_y, main_2_y;

  _2_1MUX_main main_1 (.D0(D2), .D1(S0), .S(D3), .Y(main_1_y));
  _2_1MUX_main main_2 (.D0(D0), .D1(S0), .S(D1), .Y(main_2_y));
  _2_1MUX_main main_3 (.D0(main_2_y), .D1(S1), .S(main_1_y), .Y(Y));
endmodule
