// Logisim project 4-to-grey.circ as structural Verilog: 1 circuit, main circuit main
module main (
  input  [3:0] DATA,
  output [3:0] GREY
);

  xor xor_1 (GREY[0], DATA[0], DATA[1]);
  xor xor_2 (GREY[2], DATA[2], DATA[3]);
  xor xor_3 (GREY[1], DATA[1], DATA[2]);

  assign GREY[3] = DATA[3];
endmodule
