// Logisim project 4位奇偶校验器.circ as structural Verilog: 1 circuit, main circuit main
module main (
  input  N0,
  input  N1,
  input  N2,
  input  N3,
  output ODD,
  output EVEN
);

  wire xnor_1_out, xnor_2_out, xor_1_out, xor_2_out;

  xnor xnor_1 (xnor_1_out, N0, N1);
  xnor xnor_2 (xnor_2_out, N2, N3);
  xor xor_1 (xor_1_out, N0, N1);
  xor xor_2 (xor_2_out, N2, N3);
  xnor xnor_3 (ODD, xnor_1_out, xnor_2_out);
  xor xor_3 (EVEN, xor_1_out, xor_2_out);
endmodule
