// Logisim project cmos_or.circ as structural Verilog: 2 circuits, main circuit cmos_or
module cmos_or (
  input  X,
  input  Y,
  output Z
);

  wire transistor_1_out, transistor_2_out;

  Transistor transistor_1 (.in(1'b1), .out(transistor_1_out), .gate(X));
  Transistor transistor_2 (.in(transistor_1_out), .out(transistor_2_out), .gate(Y));
  Transistor #(.\type ("n")) transistor_3 (.in(1'b0), .out(transistor_2_out), .gate(X));
  Transistor #(.\type ("n")) transistor_4 (.in(1'b0), .out(transistor_2_out), .gate(Y));
  Transistor transistor_5 (.in(1'b1), .out(Z), .gate(transistor_2_out));
  Transistor #(.\type ("n")) transistor_6 (.in(1'b0), .out(Z), .gate(transistor_2_out));

  // Notes on the sheet:
  //   或门实现电路
endmodule

module \或门  (
  input  in_1,
  input  in_2,
  output out_3
);

  wire transistor_1_out, transistor_2_out;

  Transistor transistor_1 (.in(1'b1), .out(transistor_1_out), .gate(in_1));
  Transistor transistor_2 (.in(transistor_1_out), .out(transistor_2_out), .gate(in_2));
  Transistor #(.\type ("n")) transistor_3 (.in(1'b0), .out(transistor_2_out), .gate(in_1));
  Transistor #(.\type ("n")) transistor_4 (.in(1'b0), .out(transistor_2_out), .gate(in_2));
  Transistor transistor_5 (.in(1'b1), .out(out_3), .gate(transistor_2_out));
  Transistor #(.\type ("n")) transistor_6 (.in(1'b0), .out(out_3), .gate(transistor_2_out));
endmodule
