// Logisim project lab2.5.circ as structural Verilog: 2 circuits, main circuit main
module main (
  input  [7:0] DataIn,
  input  [2:0] shamt,
  input  L_R,
  input  A_L,
  output [7:0] DataOut
);

  wire [0:0] multiplexer_2_out;
  wire [1:0] multiplexer_6_out;
  wire [3:0] multiplexer_8_out;
  wire [7:0] multiplexer_5_out, multiplexer_9_out;
  wire [7:7] multiplexer_1_out, multiplexer_3_out, multiplexer_7_out;

  Multiplexer #(.enable("false")) multiplexer_1 (.in0(1'b0), .in1(DataIn[7]), .out(multiplexer_1_out[7]), .sel(A_L));
  Multiplexer #(.enable("false")) multiplexer_2 (.in0(1'b0), .in1(DataIn[7]), .out(multiplexer_2_out[0]), .sel(A_L));
  Multiplexer #(.enable("false")) multiplexer_3 (
    .in0(1'b0), .in1(multiplexer_5_out[7]), .out(multiplexer_3_out[7]), .sel(A_L));
  Multiplexer #(.enable("false")) multiplexer_4 (
    .in0(1'b0), .in1(multiplexer_5_out[7]), .out(multiplexer_6_out[1]), .sel(A_L));
  Multiplexer #(.select(2), .width(8), .enable("false")) multiplexer_5 (
    .in0(DataIn), .in1({multiplexer_1_out[7], DataIn[7:1]}), .in2(DataIn),
    .in3({DataIn[6:0], multiplexer_2_out[0]}), .out(multiplexer_5_out), .sel({L_R, shamt[0]}));
  Multiplexer #(.enable("false")) multiplexer_6 (
    .in0(1'b0), .in1(multiplexer_5_out[6]), .out(multiplexer_6_out[0]), .sel(A_L));
  Multiplexer #(.enable("false")) multiplexer_7 (
    .in0(1'b0), .in1(multiplexer_9_out[7]), .out(multiplexer_7_out[7]), .sel(A_L));
  Multiplexer #(.enable("false")) multiplexer_8 (
    .in0(1'b0), .in1(multiplexer_9_out[4]), .out(multiplexer_8_out[0]), .sel(A_L));
  Multiplexer #(.select(2), .width(8), .enable("false")) multiplexer_9 (
    .in0(multiplexer_5_out), .in1({{2{multiplexer_3_out[7]}}, multiplexer_5_out[7:2]}),
    .in2(multiplexer_5_out), .in3({multiplexer_5_out[5:0], multiplexer_6_out}), .out(multiplexer_9_out),
    .sel({L_R, shamt[1]}));
  Multiplexer #(.enable("false")) multiplexer_10 (
    .in0(1'b0), .in1(multiplexer_9_out[5]), .out(multiplexer_8_out[1]), .sel(A_L));
  Multiplexer #(.enable("false")) multiplexer_11 (
    .in0(1'b0), .in1(multiplexer_9_out[6]), .out(multiplexer_8_out[2]), .sel(A_L));
  Multiplexer #(.enable("false")) multiplexer_12 (
    .in0(1'b0), .in1(multiplexer_9_out[7]), .out(multiplexer_8_out[3]), .sel(A_L));
  Multiplexer #(.select(2), .width(8), .enable("false")) multiplexer_13 (
    .in0(multiplexer_9_out), .in1({{4{multiplexer_7_out[7]}}, multiplexer_9_out[7:4]}),
    .in2(multiplexer_9_out), .in3({multiplexer_9_out[3:0], multiplexer_8_out}), .out(DataOut),
    .sel({L_R, shamt[2]}));

  // Other names for the same wires on the sheet: Din[7:0] = DataIn; Left_Right = L_R; Arth_Logic = A_L;
  //   Dout[7:0] = DataOut

  // Notes on the sheet:
  //   L/R,A/L: 00逻辑右移，01算术右移，10逻辑左移，11：循环左移
  //   输入引脚
  //   请勿修改引脚名称、电路名称及电路封装外观
  //   提示：使用多路选择器级联实现8位桶形移位器，禁止直接使用移位器组件。
  //   输出引脚
endmodule

module _32 (
  input  L_R,
  input  [31:0] Datain,
  input  A_L,
  input  [4:0] shamt,
  output [31:0] dataout
);

  wire [0:0] multiplexer_1_out;
  wire [1:0] multiplexer_6_out;
  wire [3:0] multiplexer_9_out;
  wire [7:0] multiplexer_15_out;
  wire [15:0] multiplexer_41_out;
  wire [31:0] multiplexer_3_out, multiplexer_8_out, multiplexer_13_out, multiplexer_23_out;
  wire [31:31] multiplexer_2_out, multiplexer_4_out, multiplexer_7_out, multiplexer_14_out,
       multiplexer_24_out;

  Multiplexer #(.enable("false")) multiplexer_1 (.in0(1'b0), .in1(Datain[31]), .out(multiplexer_1_out[0]), .sel(A_L));
  Multiplexer #(.enable("false")) multiplexer_2 (.in0(1'b0), .in1(Datain[31]), .out(multiplexer_2_out[31]), .sel(A_L));
  Multiplexer #(.select(2), .width(32), .enable("false")) multiplexer_3 (
    .in0(Datain), .in1({multiplexer_2_out[31], Datain[31:1]}), .in2(Datain),
    .in3({Datain[30:0], multiplexer_1_out[0]}), .out(multiplexer_3_out), .sel({L_R, shamt[0]}));
  Multiplexer #(.enable("false")) multiplexer_4 (
    .in0(1'b0), .in1(multiplexer_3_out[31]), .out(multiplexer_4_out[31]), .sel(A_L));
  Multiplexer #(.enable("false")) multiplexer_5 (
    .in0(1'b0), .in1(multiplexer_3_out[31]), .out(multiplexer_6_out[1]), .sel(A_L));
  Multiplexer #(.enable("false")) multiplexer_6 (
    .in0(1'b0), .in1(multiplexer_3_out[30]), .out(multiplexer_6_out[0]), .sel(A_L));
  Multiplexer #(.enable("false")) multiplexer_7 (
    .in0(1'b0), .in1(multiplexer_8_out[31]), .out(multiplexer_7_out[31]), .sel(A_L));
  Multiplexer #(.select(2), .width(32), .enable("false")) multiplexer_8 (
    .in0(multiplexer_3_out), .in1({{2{multiplexer_4_out[31]}}, multiplexer_3_out[31:2]}),
    .in2(multiplexer_3_out), .in3({multiplexer_3_out[29:0], multiplexer_6_out}), .out(multiplexer_8_out),
    .sel({L_R, shamt[1]}));
  Multiplexer #(.enable("false")) multiplexer_9 (
    .in0(1'b0), .in1(multiplexer_8_out[28]), .out(multiplexer_9_out[0]), .sel(A_L));
  Multiplexer #(.enable("false")) multiplexer_10 (
    .in0(1'b0), .in1(multiplexer_8_out[29]), .out(multiplexer_9_out[1]), .sel(A_L));
  Multiplexer #(.enable("false")) multiplexer_11 (
    .in0(1'b0), .in1(multiplexer_8_out[30]), .out(multiplexer_9_out[2]), .sel(A_L));
  Multiplexer #(.enable("false")) multiplexer_12 (
    .in0(1'b0), .in1(multiplexer_8_out[31]), .out(multiplexer_9_out[3]), .sel(A_L));
  Multiplexer #(.select(2), .width(32), .enable("false")) multiplexer_13 (
    .in0(multiplexer_8_out), .in1({{4{multiplexer_7_out[31]}}, multiplexer_8_out[31:4]}),
    .in2(multiplexer_8_out), .in3({multiplexer_8_out[27:0], multiplexer_9_out}), .out(multiplexer_13_out),
    .sel({L_R, shamt[2]}));
  Multiplexer #(.enable("false")) multiplexer_14 (
    .in0(1'b0), .in1(multiplexer_13_out[31]), .out(multiplexer_14_out[31]), .sel(A_L));
  Multiplexer #(.enable("false")) multiplexer_15 (
    .in0(1'b0), .in1(multiplexer_13_out[24]), .out(multiplexer_15_out[0]), .sel(A_L));
  Multiplexer #(.enable("false")) multiplexer_16 (
    .in0(1'b0), .in1(multiplexer_13_out[28]), .out(multiplexer_15_out[4]), .sel(A_L));
  Multiplexer #(.enable("false")) multiplexer_17 (
    .in0(1'b0), .in1(multiplexer_13_out[25]), .out(multiplexer_15_out[1]), .sel(A_L));
  Multiplexer #(.enable("false")) multiplexer_18 (
    .in0(1'b0), .in1(multiplexer_13_out[29]), .out(multiplexer_15_out[5]), .sel(A_L));
  Multiplexer #(.enable("false")) multiplexer_19 (
    .in0(1'b0), .in1(multiplexer_13_out[26]), .out(multiplexer_15_out[2]), .sel(A_L));
  Multiplexer #(.enable("false")) multiplexer_20 (
    .in0(1'b0), .in1(multiplexer_13_out[30]), .out(multiplexer_15_out[6]), .sel(A_L));
  Multiplexer #(.enable("false")) multiplexer_21 (
    .in0(1'b0), .in1(multiplexer_13_out[27]), .out(multiplexer_15_out[3]), .sel(A_L));
  Multiplexer #(.enable("false")) multiplexer_22 (
    .in0(1'b0), .in1(multiplexer_13_out[31]), .out(multiplexer_15_out[7]), .sel(A_L));
  Multiplexer #(.select(2), .width(32), .enable("false")) multiplexer_23 (
    .in0(multiplexer_13_out), .in1({{8{multiplexer_14_out[31]}}, multiplexer_13_out[31:8]}),
    .in2(multiplexer_13_out), .in3({multiplexer_13_out[23:0], multiplexer_15_out}), .out(multiplexer_23_out),
    .sel({L_R, shamt[3]}));
  Multiplexer #(.enable("false")) multiplexer_24 (
    .in0(1'b0), .in1(multiplexer_23_out[31]), .out(multiplexer_24_out[31]), .sel(A_L));
  Multiplexer #(.enable("false")) multiplexer_25 (
    .in0(1'b0), .in1(multiplexer_23_out[31]), .out(multiplexer_41_out[15]), .sel(A_L));
  Multiplexer #(.enable("false")) multiplexer_26 (
    .in0(1'b0), .in1(multiplexer_23_out[27]), .out(multiplexer_41_out[11]), .sel(A_L));
  Multiplexer #(.enable("false")) multiplexer_27 (
    .in0(1'b0), .in1(multiplexer_23_out[23]), .out(multiplexer_41_out[7]), .sel(A_L));
  Multiplexer #(.enable("false")) multiplexer_28 (
    .in0(1'b0), .in1(multiplexer_23_out[19]), .out(multiplexer_41_out[3]), .sel(A_L));
  Multiplexer #(.enable("false")) multiplexer_29 (
    .in0(1'b0), .in1(multiplexer_23_out[30]), .out(multiplexer_41_out[14]), .sel(A_L));
  Multiplexer #(.enable("false")) multiplexer_30 (
    .in0(1'b0), .in1(multiplexer_23_out[26]), .out(multiplexer_41_out[10]), .sel(A_L));
  Multiplexer #(.enable("false")) multiplexer_31 (
    .in0(1'b0), .in1(multiplexer_23_out[22]), .out(multiplexer_41_out[6]), .sel(A_L));
  Multiplexer #(.enable("false")) multiplexer_32 (
    .in0(1'b0), .in1(multiplexer_23_out[18]), .out(multiplexer_41_out[2]), .sel(A_L));
  Multiplexer #(.select(2), .width(32), .enable("false")) multiplexer_33 (
    .in0(multiplexer_23_out), .in1({{16{multiplexer_24_out[31]}}, multiplexer_23_out[31:16]}),
    .in2(multiplexer_23_out), .in3({multiplexer_23_out[15:0], multiplexer_41_out}), .out(dataout),
    .sel({L_R, shamt[4]}));
  Multiplexer #(.enable("false")) multiplexer_34 (
    .in0(1'b0), .in1(multiplexer_23_out[29]), .out(multiplexer_41_out[13]), .sel(A_L));
  Multiplexer #(.enable("false")) multiplexer_35 (
    .in0(1'b0), .in1(multiplexer_23_out[25]), .out(multiplexer_41_out[9]), .sel(A_L));
  Multiplexer #(.enable("false")) multiplexer_36 (
    .in0(1'b0), .in1(multiplexer_23_out[21]), .out(multiplexer_41_out[5]), .sel(A_L));
  Multiplexer #(.enable("false")) multiplexer_37 (
    .in0(1'b0), .in1(multiplexer_23_out[17]), .out(multiplexer_41_out[1]), .sel(A_L));
  Multiplexer #(.enable("false")) multiplexer_38 (
    .in0(1'b0), .in1(multiplexer_23_out[28]), .out(multiplexer_41_out[12]), .sel(A_L));
  Multiplexer #(.enable("false")) multiplexer_39 (
    .in0(1'b0), .in1(multiplexer_23_out[24]), .out(multiplexer_41_out[8]), .sel(A_L));
  Multiplexer #(.enable("false")) multiplexer_40 (
    .in0(1'b0), .in1(multiplexer_23_out[20]), .out(multiplexer_41_out[4]), .sel(A_L));
  Multiplexer #(.enable("false")) multiplexer_41 (
    .in0(1'b0), .in1(multiplexer_23_out[16]), .out(multiplexer_41_out[0]), .sel(A_L));

  // Other names for the same wires on the sheet: Din[31:0] = Datain; Dout[31:0] = dataout

  // Notes on the sheet:
  //   上：右移，下：左移
endmodule
