// Logisim project 思考题1（时间换空间版）.circ as structural Verilog: 2 circuits, main circuit 32位乘法器
// 加法器
module main (
  input  Cin,
  input  [31:0] X,
  input  [31:0] Y,
  output OF,
  output Cout,
  output CF,
  output ZF,
  output [31:0] S,
  output SF
);

  wire and_1_out, and_2_out, main_1_c16;

  lab4_2_main main_1 (.X(X[15:0]), .Y(Y[15:0]), .C0(Cin), .S(S[15:0]), .C16(main_1_c16));  // open: Pg, Gg
  lab4_2_main main_2 (.X(X[31:16]), .Y(Y[31:16]), .C0(main_1_c16), .S(S[31:16]), .C16(Cout));  // open: Pg, Gg
  and and_1 (and_1_out, ~Y[31], ~X[31], S[31]);  // AND_Gate
  or or_1 (OF, and_1_out, and_2_out);
  and and_2 (and_2_out, X[31], Y[31], ~S[31]);  // AND_Gate
  xor xor_1 (CF, Cout, Cin);
  Comparator #(.width(32)) comparator_1 (.a(S), .b({32{1'b0}}), .eq(ZF));  // open: gt, lt
  // Probe on X
  // Probe on Y
  // Probe on S

  assign SF = S[31];

  // Notes on the sheet:
  //   Cin: pull=down
  //   Y: pull=down
  //   X: pull=down
  //   输入引脚区
  //   输出引脚区
  //   请勿修改引脚名称、电路名称及电路封装外观
  //   提示：使用两个16位并行加法器子电路串行实现32位快速加法器
  //   功能说明:32位Adder  S=X+Y，Cout为最高位进位位，Cin为进位输入， S为和，溢出OF、进位CF、零ZF、符号SF。
  //   +
  //   =
  //   无符号加法
endmodule

module \_32位乘法器  (
  input  in_1,
  input  [31:0] in_2,
  input  [31:0] in_3,
  output [31:0] out_4
);

  wire CLK, LOAD, multiplexer_3_out, not_1_out, STOP;
  wire [5:0] counter_1_q;
  wire [31:0] main_1_s, multiplexer_1_out, multiplexer_2_out, register_1_q;
  wire [31:31] main_1_cout;

  Clock clock_1 (.out(CLK));
  Multiplexer #(.width(32), .enable("false")) multiplexer_1 (
    .in0({32{1'b0}}), .in1(in_2), .out(multiplexer_1_out), .sel(out_4[0]));
  not not_1 (not_1_out, STOP);
  main main_1 (
    .Cin(1'b0), .Cout(main_1_cout[31]), .X(multiplexer_1_out), .Y(register_1_q), .S(main_1_s));  // open: OF, CF, ZF, SF
  Register #(.width(32), .Select("low")) register_1 (
    .D({main_1_cout[31], main_1_s[31:1]}), .en(not_1_out), .Q(register_1_q), .clk(CLK), .clr(in_1));
  Multiplexer #(.width(32), .enable("false")) multiplexer_2 (
    .in0({main_1_s[0], out_4[31:1]}), .in1(in_3), .out(multiplexer_2_out), .sel(LOAD));
  Register #(.width(32), .Select("low")) register_2 (
    .D(multiplexer_2_out), .en(not_1_out), .Q(out_4), .clk(CLK), .clr(in_1));
  // Probe on in_2
  // Probe on in_3
  // Probe on out_4
  Multiplexer #(.enable("false")) multiplexer_3 (.in0(not_1_out), .in1(1'b1), .out(multiplexer_3_out), .sel(in_1));
  Counter #(.width(6), .max('h3f)) counter_1 (
    .load(in_1), .D({6{1'b0}}), .count(multiplexer_3_out), .Q(counter_1_q), .clk(CLK));  // open: carry, clr, preset, down
  Comparator #(.width(6), .mode("unsigned")) comparator_1 (.a(counter_1_q), .b({6{1'b0}}), .eq(LOAD));  // open: gt, lt
  Comparator #(.width(6), .mode("unsigned")) comparator_2 (.a(counter_1_q), .b(6'b100001), .eq(STOP));  // open: gt, lt

  // Other names for the same wires on the sheet: RST = in_1; X[31:0] = in_2; Y[31:0] = in_3; Z[31:0] = out_4
endmodule
