// Logisim project 思考题3.circ as structural Verilog: 1 circuit, main circuit 32位除法器
module \_32位除法器  (
  input  in_1,
  input  [31:0] in_2,
  input  [31:0] in_3,
  output [31:0] out_4,
  output [31:0] out_5
);

  wire CLK, LOAD, multiplexer_3_out, not_1_out, STOP, subtractor_1_bout;
  wire [0:0] not_2_out;
  wire [5:0] counter_1_q;
  wire [30:0] bit_extender_1_out, multiplexer_1_out;
  wire [31:0] bit_extender_2_out, multiplexer_2_out, register_1_q, subtractor_1_out;

  Clock clock_1 (.out(CLK));
  Bit_Extender #(.in_width(32), .out_width(31), .\type ("zero")) bit_extender_1 (
    .in(subtractor_1_out), .out(bit_extender_1_out));
  not not_1 (not_1_out, STOP);
  Subtractor #(.width(32)) subtractor_1 (
    .a(register_1_q), .b(in_3), .out(subtractor_1_out), .bout(subtractor_1_bout));  // open: bin
  Multiplexer #(.width(31), .enable("false")) multiplexer_1 (
    .in0(bit_extender_1_out), .in1(register_1_q[30:0]), .out(multiplexer_1_out), .sel(subtractor_1_bout));
  assign bit_extender_2_out = {{1{1'b0}}, multiplexer_1_out};  // Bit_Extender bit_extender_2
  Register #(.width(32), .Select("low")) register_1 (
    .D({multiplexer_1_out, out_4[31]}), .en(not_1_out), .Q(register_1_q), .clk(CLK), .clr(in_1));
  not not_2 (not_2_out[0], subtractor_1_bout);
  Register #(.width(32), .Select("low")) register_2 (
    .D(bit_extender_2_out), .en(not_1_out), .Q(out_5), .clk(CLK), .clr(in_1));
  Multiplexer #(.width(32), .enable("false")) multiplexer_2 (
    .in0({out_4[30:0], not_2_out[0]}), .in1(in_2), .out(multiplexer_2_out), .sel(LOAD));
  Register #(.width(32), .Select("low")) register_3 (
    .D(multiplexer_2_out), .en(not_1_out), .Q(out_4), .clk(CLK), .clr(in_1));
  Multiplexer #(.enable("false")) multiplexer_3 (.in0(not_1_out), .in1(1'b1), .out(multiplexer_3_out), .sel(in_1));
  Counter #(.width(6), .max('h3f)) counter_1 (
    .load(in_1), .D({6{1'b0}}), .count(multiplexer_3_out), .Q(counter_1_q), .clk(CLK));  // open: carry, clr, preset, down
  // Probe on in_2
  // Probe on in_3
  // Probe on out_4
  Comparator #(.width(6), .mode("unsigned")) comparator_1 (.a(counter_1_q), .b({6{1'b0}}), .eq(LOAD));  // open: gt, lt
  Comparator #(.width(6), .mode("unsigned")) comparator_2 (.a(counter_1_q), .b(6'b100010), .eq(STOP));  // open: gt, lt
  // Probe on out_5

  // Other names for the same wires on the sheet: RST = in_1; X[31:0] = in_2; Y[31:0] = in_3; Z[31:0] = out_4;
  //   余数[31:0] = out_5
endmodule
