// Logisim project lab5.5.circ as structural Verilog: 3 circuits, main circuit main
module Branch (
  input  [2:0] Branch,
  input  Zero,
  input  Result0,
  output NxtASrc,
  output NxtBSrc
);

  wire not_1_out;

  not not_1 (not_1_out, Zero);
  Multiplexer #(.select(3), .enable("false")) multiplexer_1 (
    .in0(1'b0), .in1(1'b1), .in2(1'b1), .in4(Zero), .in5(not_1_out), .in6(Result0), .in7(Zero),
    .out(NxtBSrc), .sel(Branch));  // open: in3
  Multiplexer #(.select(3), .enable("false")) multiplexer_2 (
    .in0(1'b0), .in1(1'b0), .in2(1'b1), .in4(1'b0), .in5(1'b0), .in6(1'b0), .in7(1'b0), .out(NxtASrc),
    .sel(Branch));  // open: in3

  // Notes on the sheet:
  //   Branch: pull=down
  //   Zero: pull=down
  //   输入信号
  //   请勿修改引脚名称、电路名称及电路封装外观
  //   不要修改控制信号的编码定义、引脚名称和在布局中的位置。
  //   输出信号
endmodule

module main (
  input  [2:0] ExtOp,
  input  [2:0] MemOp,
  input  RegWr,
  input  ALUASrc,
  input  MemWr,
  input  [1:0] ALUBSrc,
  input  [31:0] Initial_Address,
  input  [3:0] ALUctr,
  input  MemToReg,
  input  [2:0] Branch,
  input  clk,
  input  ReSet,
  output [31:0] PC,
  output [31:0] BusW,
  output [31:0] Din,
  output NxtASrc,
  output NxtBSrc
);

  wire alu_1_zero;
  wire [31:0] alu_1_s, dataram_1_dataout, idu_1_busa, idu_1_busb, idu_1_dataa, idu_1_datab, idu_1_imm,
       rom_1_data;

  IFU ifu_1 (
    .CLK(clk), .Reset(ReSet), .NxtASrc(NxtASrc), .NxtBSrc(NxtBSrc), .Initial_Address(Initial_Address),
    .Imm(idu_1_imm), .BusA(idu_1_busa), .PC(PC));
  ROM #(.addrWidth(16), .dataWidth(32), .Select("low")) rom_1 (.addr(PC[17:2]), .data(rom_1_data));
  IDU idu_1 (
    .ExtOp(ExtOp), .RegWr(RegWr), .ALUASrc(ALUASrc), .ALUBSrc(ALUBSrc), .IR(rom_1_data), .BusW(BusW),
    .PC(PC), .DataA(idu_1_dataa), .BusB(idu_1_busb), .DataB(idu_1_datab), .Imm(idu_1_imm), .BusA(idu_1_busa),
    .CLK(clk));  // open: OpCode, Funct3, Funct7
  Branch branch_1 (.Branch(Branch), .NxtASrc(NxtASrc), .Zero(alu_1_zero), .NxtBSrc(NxtBSrc), .Result0(alu_1_s[0]));
  ALU alu_1 (.A(idu_1_dataa), .B(idu_1_datab), .S(alu_1_s), .ALUctr(ALUctr), .Zero(alu_1_zero));
  Multiplexer #(.width(32), .enable("false")) multiplexer_1 (.in0(idu_1_busb), .out(Din), .sel(ReSet));  // open: in1
  DataRam dataram_1 (
    .CLK(clk), .WE(MemWr), .MemOp(MemOp), .Addr(alu_1_s[17:0]), .Din(Din), .DataOut(dataram_1_dataout));  // open: CLR, AlignErr
  Multiplexer #(.width(32), .enable("false")) multiplexer_2 (
    .in0(alu_1_s), .in1(dataram_1_dataout), .out(BusW), .sel(MemToReg));

  // Other names for the same wires on the sheet: Init_Addr[31:0] = Initial_Address

  // Notes on the sheet:
  //   NxtBSrc: pull=down
  //   RegWr: pull=down
  //   ExtOp: pull=down
  //   NxtASrc: pull=down
  //   ALUctr: pull=down
  //   Branch: pull=down
  //   ALUBSrc: pull=down
  //   ALUASrc: pull=down
  //   输入信号
  //   contents of rom_1 (hex, n*v repeats v):
  //   256*0 fedca2b7 f9c28293 1006013 6502223 6400303 6601423 6405383 6701623 4042d413 6444b3 649533
  //   8505b3 b2a633 b2b6b3 40b287b3 6f02823 67c263 67d263 40086f 4808e7 1917
  //   请勿修改引脚名称、电路名称及电路封装外观
  //   为了后续实验中的引用，不要修改控制信号的编码定义、引脚名称和在布局中的位置。
  //   指令存储器和数据存储器数据位都是32位，指令存储器编址以字为单位，数据存储器编址以字节为单位。
  //   32位数据存储器，按字节分4片存储，可按照字节、半字和字进行存储；读取字节或半字时，支持0扩展和符号位扩展。
  //   输出信号
endmodule

module IFU (
  input  [31:0] Initial_Address,
  input  [31:0] Imm,
  input  [31:0] BusA,
  input  CLK,
  input  Reset,
  input  NxtASrc,
  input  NxtBSrc,
  output [31:0] PC
);

  wire [31:0] adder_1_out, multiplexer_1_out, multiplexer_2_out, multiplexer_3_out;

  Multiplexer #(.width(32), .enable("false")) multiplexer_1 (
    .in0(PC), .in1(BusA), .out(multiplexer_1_out), .sel(NxtASrc));
  Multiplexer #(.width(32), .enable("false")) multiplexer_2 (
    .in0(32'h4), .in1(Imm), .out(multiplexer_2_out), .sel(NxtBSrc));
  Adder #(.width(32)) adder_1 (.a(multiplexer_1_out), .b(multiplexer_2_out), .out(adder_1_out));  // open: cin, cout
  Multiplexer #(.width(32), .enable("false")) multiplexer_3 (
    .in0(adder_1_out), .in1(Initial_Address), .out(multiplexer_3_out), .sel(Reset));
  Register #(.width(32), .Select("low")) register_1 (.D(multiplexer_3_out), .Q(PC), .clk(CLK));  // open: en, clr
  ROM #(.addrWidth(16), .dataWidth(32), .Select("high")) rom_1 (.addr(PC[17:2]));  // open: data

  // Other names for the same wires on the sheet: Init_Addr[31:0] = Initial_Address

  // Notes on the sheet:
  //   BusA: pull=down
  //   NxtBSrc: pull=down
  //   Imm: pull=down
  //   NxtASrc: pull=down
  //   输入信号
  //   请勿修改引脚名称、电路名称及电路封装外观
  //   指令存储器256KB，数据位为32位，地址位为16位。PC寄存器数据宽度32位，片选信号高电平有效
  //   输出信号
  //   contents of rom_1 (hex, n*v repeats v):
  //   256*0 2083 8133 106213 406293 fff06313 4410663 106193 406393 806413 21b5b3 2058063 3a483 42503
  //   a4b5b3 458c63 a3a023 942023 c0006f 610133 fc9ff06f 4181b3 5383b3 540433 fc9ff06f 6f 0 0 413 9117
  //   ffc10113 94000ef 50463 8067 ff010113 100513 112623 74000ef ff010113 812423 912223 15c00413 1212023
  //   112623 c400493 9840913 442783 42703 4a503 440413 e787b3 40f50533 153513 f42223 448493 fa5ff0ef
  //   fd241ce3 100513 f99ff0ef c12083 812403 412483 12903 513 1010113 8067 1ea02e23 6f ff010113 b800513
  //   112623 f7dff0ef 1ea02e23 6f 0 1 1 2 3 5 8 d 15 22 37 59 90 e9 179 262 3db 63d a18 1055 1a6d 2ac2
  //   452f 6ff1 b520 12511 1da31 2ff42 4d973 7d8b5 cb228 148add 213d05 35c7e2 5704e7 8cccc9 e3d1b0 1709e79
  //   2547029 3c50ea2 6197ecb 1 1 deadbeef 395*0 413 9117 ffc10113 ec000ef 50463 8067 ff010113 100513
  //   112623 cc000ef ff010113 19400813 112623 812423 912223 1212023 100793 f82223 f82023 880593 7c80313
  //   100713 19800513 100893 50493 50793 100693 80006f 7a703 d70633 c7a023 478793 70693 feb796e3 117a023
  //   478593 658663 482703 fc9ff06f 11400413 7c40913 100793 c0006f 4a783 448493 42503 440413 40f50533
  //   153513 f4dff0ef fe8912e3 100513 f41ff0ef c12083 812403 412483 12903 513 1010113 8067 18a02823 6f
  //   ff010113 11000513 112623 f25ff0ef 18a02823 6f 0 1 1e 1b3 fdc 6b0d 22caa 90f6f 1f1058 594efd da4f4e
  //   1ca7357 3418be4 527c829 72363ea 8aaf953 93ee7d0 8aaf953 72363ea 527c829 3418be4 1ca7357 da4f4e
  //   594efd 1f1058 90f6f 22caa 6b0d fdc 1b3 1e 1 2 3 4 5 6 7 8 9 a b c d e f 10 11 12 13 14 15 16 17 18
  //   19 1a 1b 1c 1d 1e 1f deadbeef deadbeef 444*0 413 9117 ffc10113 39c000ef 50463 8067 ff010113 100513
  //   112623 380000ef 259693 d506b3 50893 6a803 60513 6c5dc63 261793 f887b3 7a783 fff50613 261613 c88633
  //   140006f fff50513 472783 6b50863 70613 ffc60713 fef846e3 259693 d886b3 251313 f6a023 688633 4a5de63
  //   68713 c0006f 158593 2a58463 72783 70693 470713 fef856e3 f62023 f8a5cee3 58513 106a023 8067 6886b3
  //   6a783 f62023 106a023 8067 251693 d886b3 f6a023 fe9ff06f 58513 fe1ff06f 1ec5da63 fa010113 4812c23
  //   5612023 3812c23 4112e23 4912a23 5212823 5312623 5412423 5512223 3712e23 3912a23 3a12823 3b12623
  //   58c13 60b13 50413 b0613 c0593 40513 ee9ff0ef a12223 fff50c93 159c5663 c8613 c0593 40513 ecdff0ef
  //   a12423 fff50d13 13ac5263 d0613 c0593 40513 eb1ff0ef a12623 fff50d93 fbc5e63 d8613 c0593 40513
  //   e95ff0ef a12823 fff50993 d3c5a63 98613 c0593 40513 e79ff0ef fff50913 50493 b2c5863 90613 c0593 40513
  //   e5dff0ef fff50b93 50a13 97c5663 b8613 c0593 40513 e41ff0ef a12a23 fff50a93 75c5263 a8613 c0593 40513
  //   e25ff0ef fff50693 50713 4dc5063 68613 c0593 40513 e12e23 d12c23 e01ff0ef 50813 c0593 fff50613 40513
  //   180c13 eadff0ef 1812683 1c12703 fcdc44e3 170c13 fb5c42e3 1412783 178c13 f77c4ee3 1a0c13 f52c4ce3
  //   148c13 f33c4ae3 1012783 178c13 f1bc46e3 c12783 178c13 efac42e3 812783 178c13 eb9c4ee3 412783 178c13
  //   e96c4ae3 5c12083 5812403 5412483 5012903 4c12983 4812a03 4412a83 4012b03 3c12b83 3812c03 3412c83
  //   3012d03 2c12d83 6010113 8067 8067 fe010113 1412423 1300613 593 3c000513 812c23 912a23 1212823
  //   1312623 112e23 3c000493 dddff0ef 3c000913 413 1400993 92503 490913 40850533 153513 140413 cddff0ef
  //   ff3414e3 100513 cd1ff0ef 1300613 593 3c000513 d9dff0ef 413 1400913 4a503 448493 40850533 153513
  //   140413 ca1ff0ef ff2414e3 100513 c95ff0ef 1c12083 1812403 1412483 1012903 c12983 812a03 513 2010113
  //   8067 6f ff010113 3bc00513 112623 f31ff0ef 6f 0 2 c e 6 d f 10 a 0 12 b 13 9 1 7 5 4 3 8 11 deadbeef
  //   deadbeef 63658*0 413 9117 ffc10113 39c000ef 50463 8067 ff010113 100513 112623 380000ef 259693 d506b3
  //   50893 6a803 60513 6c5dc63 261793 f887b3 7a783 fff50613 261613 c88633 140006f fff50513 472783 6b50863
  //   70613 ffc60713 fef846e3 259693 d886b3 251313 f6a023 688633 4a5de63 68713 c0006f 158593 2a58463 72783
  //   70693 470713 fef856e3 f62023 f8a5cee3 58513 106a023 8067 6886b3 6a783 f62023 106a023 8067 251693
  //   d886b3 f6a023 fe9ff06f 58513 fe1ff06f 1ec5da63 fa010113 4812c23 5612023 3812c23 4112e23 4912a23
  //   5212823 5312623 5412423 5512223 3712e23 3912a23 3a12823 3b12623 58c13 60b13 50413 b0613 c0593 40513
  //   ee9ff0ef a12223 fff50c93 159c5663 c8613 c0593 40513 ecdff0ef a12423 fff50d13 13a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
endmodule
