// Logisim project lab6.1.circ as structural Verilog: 1 circuit, main circuit 控制器
module \控制器  (
  input  [6:0] opcode,
  input  [2:0] funct3,
  input  [6:0] funct7,
  output [2:0] ExtOp,
  output RegWr,
  output [2:0] Branch,
  output ALUASrc,
  output [1:0] ALUBSrc,
  output [3:0] ALUctr,
  output MemtoReg,
  output [2:0] MemOp,
  output MemWr
);

  wire and_1_out, and_2_out, and_3_out, and_4_out, and_5_out, and_6_out, and_7_out, and_8_out, and_9_out,
       and_10_out, and_11_out, and_12_out, and_13_out, and_14_out, and_15_out, and_16_out, and_17_out,
       and_18_out, and_19_out, and_20_out, and_21_out, and_22_out, and_23_out, and_24_out, and_25_out,
       and_26_out, and_27_out, and_28_out, and_29_out, and_30_out, and_31_out, and_32_out, and_33_out,
       and_34_out, and_35_out, and_36_out, and_37_out, comparator_6_eq, comparator_7_eq, comparator_8_eq,
       comparator_9_eq, comparator_10_eq, comparator_11_eq, comparator_12_eq, comparator_13_eq,
       comparator_14_eq, comparator_14_gt, comparator_15_eq, comparator_15_gt, comparator_16_eq,
       comparator_17_eq, comparator_18_eq, comparator_19_eq, comparator_20_eq, comparator_21_eq,
       comparator_22_eq, comparator_23_eq, comparator_28_eq, comparator_29_eq, comparator_30_eq,
       comparator_31_eq, comparator_32_eq, comparator_33_eq, comparator_34_eq, comparator_35_eq,
       comparator_36_eq, comparator_37_eq, comparator_38_eq, comparator_41_eq, comparator_42_eq,
       comparator_43_eq, comparator_44_eq, comparator_45_eq, comparator_46_eq, comparator_47_eq, I_Arith,
       J_Jalr, or_1_out, or_2_out, or_7_out, or_8_out, or_9_out, or_13_out, or_14_out, or_15_out, or_16_out,
       or_22_out, or_23_out, or_24_out, or_25_out, or_27_out, R_Arith, U_auipc, U_lui;

  Comparator #(.width(7), .mode("unsigned")) comparator_1 (.a(opcode), .b(7'b0100011), .eq(MemWr));  // open: gt, lt
  Comparator #(.width(7), .mode("unsigned")) comparator_2 (.a(opcode), .b(7'b0110111), .eq(U_lui));  // open: gt, lt
  Comparator #(.width(7), .mode("unsigned")) comparator_3 (.a(opcode), .b(7'b0000011), .eq(MemtoReg));  // open: gt, lt
  Comparator #(.width(7), .mode("unsigned")) comparator_4 (.a(opcode), .b(7'b0010111), .eq(U_auipc));  // open: gt, lt
  Comparator #(.width(7), .mode("unsigned")) comparator_5 (.a(opcode), .b(7'b1100011), .eq(Branch[2]));  // open: gt, lt
  Comparator #(.width(3), .mode("unsigned")) comparator_6 (
    .a(funct3), .b(3'b001), .eq(comparator_6_eq));  // open: gt, lt
  Comparator #(.width(1), .mode("unsigned")) comparator_7 (
    .a(funct7[5]), .b(1'b0), .eq(comparator_7_eq));  // open: gt, lt
  Comparator #(.width(3), .mode("unsigned")) comparator_8 (
    .a(funct3), .b(3'b101), .eq(comparator_8_eq));  // open: gt, lt
  Comparator #(.width(1), .mode("unsigned")) comparator_9 (
    .a(funct7[5]), .b(1'b1), .eq(comparator_9_eq));  // open: gt, lt
  Comparator #(.width(3), .mode("unsigned")) comparator_10 (
    .a(funct3), .b(3'b001), .eq(comparator_10_eq));  // open: gt, lt
  Comparator #(.width(1), .mode("unsigned")) comparator_11 (
    .a(funct7[5]), .b(1'b0), .eq(comparator_11_eq));  // open: gt, lt
  Comparator #(.width(1), .mode("unsigned")) comparator_12 (
    .a(funct7[5]), .b(1'b1), .eq(comparator_12_eq));  // open: gt, lt
  Comparator #(.width(3), .mode("unsigned")) comparator_13 (
    .a(funct3), .b(3'b011), .eq(comparator_13_eq));  // open: gt, lt
  Comparator #(.width(3), .mode("unsigned")) comparator_14 (
    .a(funct3), .b(3'b101), .gt(comparator_14_gt), .eq(comparator_14_eq));  // open: lt
  Comparator #(.width(3), .mode("unsigned")) comparator_15 (
    .a(funct3), .b(3'b111), .gt(comparator_15_gt), .eq(comparator_15_eq));  // open: lt
  Comparator #(.width(3), .mode("unsigned")) comparator_16 (
    .a(funct3), .b(3'b001), .eq(comparator_16_eq));  // open: gt, lt
  or or_1 (or_1_out, comparator_16_eq, comparator_17_eq, comparator_18_eq);
  Comparator #(.width(3), .mode("unsigned")) comparator_17 (
    .a(funct3), .b(3'b101), .eq(comparator_17_eq));  // open: gt, lt
  Comparator #(.width(3), .mode("unsigned")) comparator_18 (
    .a(funct3), .b(3'b111), .eq(comparator_18_eq));  // open: gt, lt
  Comparator #(.width(3), .mode("unsigned")) comparator_19 (
    .a(funct3), .b(3'b100), .eq(comparator_19_eq));  // open: gt, lt
  or or_2 (or_2_out, comparator_19_eq, comparator_17_eq, comparator_18_eq, comparator_20_eq);
  Comparator #(.width(3), .mode("unsigned")) comparator_20 (
    .a(funct3), .b(3'b110), .eq(comparator_20_eq));  // open: gt, lt
  Comparator #(.width(3), .mode("unsigned")) comparator_21 (
    .a(funct3), .b(3'b110), .eq(comparator_21_eq));  // open: gt, lt
  Comparator #(.width(3), .mode("unsigned")) comparator_22 (
    .a(funct3), .b(3'b011), .eq(comparator_22_eq));  // open: gt, lt
  Comparator #(.width(3), .mode("unsigned")) comparator_23 (
    .a(funct3), .b(3'b111), .eq(comparator_23_eq));  // open: gt, lt
  and and_1 (and_1_out, comparator_6_eq, comparator_7_eq);
  and and_2 (and_2_out, comparator_7_eq, comparator_8_eq);
  and and_3 (and_3_out, comparator_8_eq, comparator_9_eq);
  or or_3 (RegWr, U_auipc, I_Arith, R_Arith, U_lui, MemtoReg, J_Jalr, ExtOp[2]);
  or or_4 (ALUASrc, U_auipc, J_Jalr, ExtOp[2]);
  or or_5 (ALUBSrc[0], J_Jalr, ExtOp[2]);
  or or_6 (ALUBSrc[1], MemWr, U_lui, U_auipc, I_Arith, MemtoReg);
  or or_7 (or_7_out, comparator_21_eq, comparator_23_eq);
  and and_4 (and_4_out, comparator_10_eq, comparator_11_eq);
  and and_5 (and_5_out, comparator_11_eq, comparator_13_eq);
  and and_6 (and_6_out, comparator_11_eq, comparator_14_eq);
  and and_7 (and_7_out, comparator_12_eq, comparator_14_eq);
  and and_8 (and_8_out, comparator_15_eq, comparator_11_eq);
  Comparator #(.width(7), .mode("unsigned")) comparator_24 (.a(opcode), .b(7'b0010011), .eq(I_Arith));  // open: gt, lt
  Comparator #(.width(7), .mode("unsigned")) comparator_25 (.a(opcode), .b(7'b1100111), .eq(J_Jalr));  // open: gt, lt
  and and_9 (and_9_out, or_1_out, Branch[2]);
  and and_10 (and_10_out, or_2_out, Branch[2]);
  or or_8 (or_8_out, comparator_22_eq, comparator_23_eq, and_1_out, and_2_out, and_3_out);
  or or_9 (or_9_out, and_4_out, and_5_out, and_6_out, and_7_out, and_8_out);
  or or_10 (Branch[0], ExtOp[2], and_9_out);
  or or_11 (Branch[1], J_Jalr, and_10_out);
  and and_11 (and_11_out, or_7_out, Branch[2]);
  and and_12 (and_12_out, or_8_out, I_Arith);
  and and_13 (and_13_out, or_9_out, R_Arith);
  Comparator #(.width(7), .mode("unsigned")) comparator_26 (.a(opcode), .b(7'b0110011), .eq(R_Arith));  // open: gt, lt
  Comparator #(.width(7), .mode("unsigned")) comparator_27 (.a(opcode), .b(7'b1101111), .eq(ExtOp[2]));  // open: gt, lt
  Comparator #(.width(3), .mode("unsigned")) comparator_28 (
    .a(funct3), .b(3'b100), .eq(comparator_28_eq));  // open: gt, lt
  Comparator #(.width(3), .mode("unsigned")) comparator_29 (
    .a(funct3), .b(3'b000), .eq(comparator_29_eq));  // open: gt, lt
  Comparator #(.width(3), .mode("unsigned")) comparator_30 (
    .a(funct3), .b(3'b001), .eq(comparator_30_eq));  // open: gt, lt
  Comparator #(.width(3), .mode("unsigned")) comparator_31 (
    .a(funct3), .b(3'b101), .eq(comparator_31_eq));  // open: gt, lt
  or or_12 (ALUctr[0], and_12_out, U_lui, and_13_out, and_11_out);
  or or_13 (or_13_out, comparator_28_eq, comparator_29_eq);
  or or_14 (or_14_out, comparator_30_eq, comparator_31_eq);
  or or_15 (or_15_out, comparator_29_eq, comparator_30_eq);
  or or_16 (or_16_out, comparator_29_eq, comparator_30_eq);
  and and_14 (and_14_out, or_13_out, MemtoReg);
  or or_17 (MemOp[0], and_14_out, and_15_out);
  and and_15 (and_15_out, comparator_29_eq, MemWr);
  and and_16 (and_16_out, or_14_out, MemtoReg);
  or or_18 (MemOp[1], and_16_out, and_17_out);
  and and_17 (and_17_out, comparator_30_eq, MemWr);
  and and_18 (and_18_out, or_15_out, MemtoReg);
  or or_19 (MemOp[2], and_18_out, and_19_out);
  and and_19 (and_19_out, or_16_out, MemWr);
  Comparator #(.width(1), .mode("unsigned")) comparator_32 (
    .a(funct7[5]), .b(1'b0), .eq(comparator_32_eq));  // open: gt, lt
  Comparator #(.width(3), .mode("unsigned")) comparator_33 (
    .a(funct3), .b(3'b010), .eq(comparator_33_eq));  // open: gt, lt
  Comparator #(.width(3), .mode("unsigned")) comparator_34 (
    .a(funct3), .b(3'b011), .eq(comparator_34_eq));  // open: gt, lt
  Comparator #(.width(3), .mode("unsigned")) comparator_35 (
    .a(funct3), .b(3'b110), .eq(comparator_35_eq));  // open: gt, lt
  Comparator #(.width(3), .mode("unsigned")) comparator_36 (
    .a(funct3), .b(3'b111), .eq(comparator_36_eq));  // open: gt, lt
  or or_20 (ExtOp[1], Branch[2], MemWr);
  or or_21 (ExtOp[0], U_lui, U_auipc, Branch[2]);
  and and_20 (and_20_out, comparator_33_eq, comparator_32_eq);
  and and_21 (and_21_out, comparator_34_eq, comparator_32_eq);
  and and_22 (and_22_out, comparator_35_eq, comparator_32_eq);
  and and_23 (and_23_out, comparator_36_eq, comparator_32_eq);
  Comparator #(.width(1), .mode("unsigned")) comparator_37 (
    .a(funct7[5]), .b(1'b1), .eq(comparator_37_eq));  // open: gt, lt
  Comparator #(.width(1), .mode("unsigned")) comparator_38 (
    .a(funct7[5]), .b(1'b0), .eq(comparator_38_eq));  // open: gt, lt
  Comparator #(.width(3), .mode("unsigned")) comparator_39 (.a(funct3), .b(3'b010));  // open: gt, eq, lt
  Comparator #(.width(3), .mode("unsigned")) comparator_40 (.a(funct3), .b(3'b011));  // open: gt, eq, lt
  Comparator #(.width(3), .mode("unsigned")) comparator_41 (
    .a(funct3), .b(3'b100), .eq(comparator_41_eq));  // open: gt, lt
  Comparator #(.width(3), .mode("unsigned")) comparator_42 (
    .a(funct3), .b(3'b110), .eq(comparator_42_eq));  // open: gt, lt
  Comparator #(.width(3), .mode("unsigned")) comparator_43 (
    .a(funct3), .b(3'b111), .eq(comparator_43_eq));  // open: gt, lt
  Comparator #(.width(3), .mode("unsigned")) comparator_44 (
    .a(funct3), .b(3'b101), .eq(comparator_44_eq));  // open: gt, lt
  or or_22 (or_22_out, comparator_33_eq, comparator_34_eq, comparator_35_eq, comparator_36_eq);
  or or_23 (or_23_out, and_20_out, and_21_out, and_22_out, and_23_out);
  and and_24 (and_24_out, or_22_out, I_Arith);
  and and_25 (and_25_out, R_Arith, or_23_out);
  and and_26 (and_26_out, comparator_41_eq, comparator_38_eq);
  and and_27 (and_27_out, comparator_44_eq, comparator_38_eq);
  and and_28 (and_28_out, comparator_44_eq, comparator_37_eq);
  and and_29 (and_29_out, comparator_42_eq, comparator_38_eq);
  and and_30 (and_30_out, comparator_43_eq, comparator_38_eq);
  or or_24 (or_24_out, comparator_42_eq, comparator_41_eq, comparator_43_eq, comparator_44_eq);
  or or_25 (or_25_out, and_26_out, and_27_out, and_28_out, and_29_out, and_30_out);
  or or_26 (ALUctr[1], Branch[2], and_24_out, and_25_out, U_lui);
  Comparator #(.width(1), .mode("unsigned")) comparator_45 (
    .a(funct7[5]), .b(1'b1), .eq(comparator_45_eq));  // open: gt, lt
  Comparator #(.width(3), .mode("unsigned")) comparator_46 (
    .a(funct3), .b(3'b000), .eq(comparator_46_eq));  // open: gt, lt
  Comparator #(.width(3), .mode("unsigned")) comparator_47 (
    .a(funct3), .b(3'b101), .eq(comparator_47_eq));  // open: gt, lt
  and and_31 (and_31_out, or_24_out, I_Arith);
  and and_32 (and_32_out, or_25_out, R_Arith);
  and and_33 (and_33_out, comparator_46_eq, comparator_45_eq);
  and and_34 (and_34_out, comparator_47_eq, comparator_45_eq);
  or or_27 (or_27_out, and_33_out, and_34_out);
  or or_28 (ALUctr[2], U_lui, and_31_out, and_32_out);
  and and_35 (and_35_out, comparator_45_eq, comparator_47_eq);
  and and_36 (and_36_out, and_35_out, I_Arith);
  and and_37 (and_37_out, or_27_out, R_Arith);
  or or_29 (ALUctr[3], U_lui, and_36_out, and_37_out);

  // Other names for the same wires on the sheet: B_Instr = Branch[2]; J_Jal = ExtOp[2]; L_Load = MemtoReg;
  //   S_Instr = MemWr

  // Notes on the sheet:
  //   输入引脚
  //   请勿修改引脚名称、电路名称及电路封装外观
  //   提示：根据指令种类，把7位指令code用一位指令类型标志位来表示，再通过功能码来区分具体指令，生成控制信号。
  //   输出引脚
endmodule
