// Logisim project lab6.2.circ as structural Verilog: 16 circuits, main circuit main
module main (
  input  ReSet,
  input  [31:0] Init_Addr,
  input  clk,
  output [31:0] PC,
  output [31:0] IR,
  output [31:0] BusW,
  output [31:0] Din,
  output [15:0] Cycles,
  output Halt
);

  wire alu_1_zero, ALUASrc, clk_out, clk_t, comparator_1_eq, MemToReg, MemWr, not_2_out, NxtASrc, NxtBSrc,
       RegWr;
  wire [1:0] ALUBSrc;
  wire [2:0] Branch, ExtOp, Funct3, MemOp;
  wire [3:0] ALUctr;
  wire [6:0] Funct7, Opcode;
  wire [31:0] adder_1_out, alu_1_s, dataram_1_dataout, idu_1_busa, idu_1_busb, idu_1_dataa, idu_1_datab,
       idu_1_imm, ifu_1_pc;

  Adder #(.width(32)) adder_1 (.a(ifu_1_pc), .b(32'h4), .out(adder_1_out));  // open: cin, cout
  Comparator #(.width(16), .mode("unsigned")) comparator_1 (
    .a(16'h150), .b(Cycles), .eq(comparator_1_eq));  // open: gt, lt
  not not_1 (clk_t, clk_out);
  Clock u_clk (.out(clk_out));
  IFU ifu_1 (
    .CLK(clk_t), .Reset(ReSet), .NxtASrc(NxtASrc), .NxtBSrc(NxtBSrc), .Initial_Address(Init_Addr),
    .Imm(idu_1_imm), .BusA(idu_1_busa), .PC(ifu_1_pc), .halt(Halt));
  Multiplexer #(.width(32), .enable("false")) multiplexer_1 (
    .in0(ifu_1_pc), .in1(adder_1_out), .out(PC), .sel(comparator_1_eq));
  \控制器  \u_控制器_1  (
    .opcode(Opcode), .ExtOp(ExtOp), .RegWr(RegWr), .Branch(Branch), .funct3(Funct3), .ALUASrc(ALUASrc),
    .ALUBSrc(ALUBSrc), .ALUctr(ALUctr), .funct7(Funct7), .MemtoReg(MemToReg), .MemOp(MemOp), .MemWr(MemWr),
    .Halt(Halt));
  ROM #(.addrWidth(16), .dataWidth(32), .Select("low")) rom_1 (.addr(ifu_1_pc[17:2]), .data(IR));
  IDU idu_1 (
    .OpCode(Opcode), .ExtOp(ExtOp), .RegWr(RegWr), .Imm(idu_1_imm), .Funct3(Funct3), .ALUASrc(ALUASrc),
    .ALUBSrc(ALUBSrc), .Funct7(Funct7), .CLK(clk_t), .IR(IR), .BusW(BusW), .PC(ifu_1_pc),
    .DataA(idu_1_dataa), .DataB(idu_1_datab), .BusA(idu_1_busa), .BusB(idu_1_busb));
  Branch branch_1 (.Branch(Branch), .NxtASrc(NxtASrc), .Zero(alu_1_zero), .NxtBSrc(NxtBSrc), .Result0(alu_1_s[0]));
  ALU alu_1 (.A(idu_1_dataa), .B(idu_1_datab), .ALUctr(ALUctr), .S(alu_1_s), .Zero(alu_1_zero));
  Multiplexer #(.width(32), .enable("false")) multiplexer_2 (.in0(idu_1_busb), .out(Din), .sel(ReSet));  // open: in1
  // Probe on Cycles
  Counter #(.width(16), .max('hffff), .behavior("old")) \u_计数器  (
    .count(not_2_out), .Q(Cycles), .clk(clk_t), .clr(ReSet));  // open: load, D, carry, preset
  not not_2 (not_2_out, Halt);
  DataRAM dataram_1 (
    .Addr(alu_1_s[17:0]), .Din(Din), .CLK(clk_t), .CLR(1'b0), .WE(MemWr), .MemOp(MemOp),
    .DataOut(dataram_1_dataout));  // open: AlignErr
  Multiplexer #(.width(32), .enable("false")) multiplexer_3 (
    .in0(alu_1_s), .in1(dataram_1_dataout), .out(BusW), .sel(MemToReg));

  // Notes on the sheet:
  //   输入引脚
  //   contents of rom_1 (hex, n*v repeats v):
  //   413 9117 ffc10113 2ec000ef 259693 d50833 50313 82883 60513 8c5d863 261793 f307b3 7a783 fff50713
  //   271713 e30733 70613 ffc70713 2f8d463 fff50513 472783 fea5c6e3 d30833 f82023 58513 f62023 1182023
  //   8067 d30833 251613 f82023 c30633 4a5d063 468713 e30733 70813 158593 470713 ffc72783 fca584e3
  //   fef8d6e3 f62023 2a5d063 259693 f85ff06f 58513 1182023 8067 58513 fa1ff06f 259813 1030833 58513
  //   f95ff06f 1ec5da63 fa010113 4812c23 5512223 3712e23 4112e23 4912a23 5212823 5312623 5412423 5612023
  //   3812c23 3912a23 3a12823 3b12623 58b93 60a93 50413 a8613 b8593 40513 ee5ff0ef a12223 fff50c93
  //   159bd663 c8613 b8593 40513 ec9ff0ef a12423 fff50d13 13abd263 d0613 b8593 40513 eadff0ef a12623
  //   fff50d93 fbbde63 d8613 b8593 40513 e91ff0ef a12823 fff50993 d3bda63 98613 b8593 40513 e75ff0ef
  //   fff50913 50493 b2bd863 90613 b8593 40513 e59ff0ef fff50b13 50a13 96bd663 b0613 b8593 40513 e3dff0ef
  //   a12a23 fff50c13 78bd263 c0613 b8593 40513 e21ff0ef fff50813 50713 50bd063 80613 b8593 40513 e12e23
  //   1012c23 dfdff0ef 50893 b8593 fff50613 40513 188b93 eadff0ef 1812803 1c12703 fd0bc4e3 170b93 fb8bc2e3
  //   1412783 178b93 f76bcee3 1a0b93 f52bcce3 148b93 f33bcae3 1012783 178b93 f1bbc6e3 c12783 178b93
  //   efabc2e3 812783 178b93 eb9bcee3 412783 178b93 e95bcae3 5c12083 5812403 5412483 5012903 4c12983
  //   4812a03 4412a83 4012b03 3c12b83 3812c03 3412c83 3012d03 2c12d83 6010113 8067 8067 ff010113 31400513
  //   1300613 593 112623 df5ff0ef c12083 513 1010113 8067 ff010113 31000513 112623 fcdff0ef 36a02223 6f 0
  //   4e20 1d4c0 53724e00 5b8d80 13d620 5dc 9896800 186a0 0 2bf20 2af8 b532b80 15f90 3e8 46 32 61a80
  //   2dc6c0 1f40 aa deadbeef
  //   请勿修改引脚名称、电路名称及电路封装外观
  //   指令存储器和数据存储器数据位都是32位，指令存储器编址以字为单位，数据存储器编址以字节为单位。
  //   引用取指令部件、取操作数部件、ALU部件、数据存储器、分支控制器、指令存储器等部件，完成单周期CPU设计。
  //   输出引脚
  //   状态元件的触发条件都设置成上升沿触发，时钟输入信号通过反相器输入。
  //   程序执行周期数
endmodule

module Branch (
  input  [2:0] Branch,
  input  Zero,
  input  Result0,
  output NxtASrc,
  output NxtBSrc
);

  wire not_1_out, not_2_out, or_1_out;

  not not_1 (not_1_out, Zero);
  not not_2 (not_2_out, Result0);
  or or_1 (or_1_out, not_2_out, Zero);
  Multiplexer #(.select(3), .enable("false")) multiplexer_1 (
    .in0(1'b0), .in1(1'b1), .in2(1'b1), .in4(Zero), .in5(not_1_out), .in6(Result0), .in7(or_1_out),
    .out(NxtBSrc), .sel(Branch));  // open: in3
  Multiplexer #(.select(3), .enable("false")) multiplexer_2 (
    .in0(1'b0), .in1(1'b0), .in2(1'b1), .in4(1'b0), .in5(1'b0), .in6(1'b0), .in7(1'b0), .out(NxtASrc),
    .sel(Branch));  // open: in3

  // Notes on the sheet:
  //   Zero: pull=down
  //   Branch: pull=down
  //   输入信号
  //   请勿修改引脚名称、电路名称及电路封装外观
  //   不要修改控制信号的编码定义、引脚名称和在布局中的位置。
  //   输出信号
endmodule

module IFU (
  input  [31:0] Initial_Address,
  input  [31:0] Imm,
  input  [31:0] BusA,
  input  CLK,
  input  Reset,
  input  halt,
  input  NxtASrc,
  input  NxtBSrc,
  output [31:0] PC
);

  wire [31:0] adder_1_out, IR, multiplexer_1_out, multiplexer_2_out, multiplexer_3_out;

  Multiplexer #(.width(32), .enable("false")) multiplexer_1 (
    .in0(PC), .in1(BusA), .out(multiplexer_1_out), .sel(NxtASrc));
  Multiplexer #(.width(32), .enable("false")) multiplexer_2 (
    .in0(32'h4), .in1(Imm), .out(multiplexer_2_out), .sel(NxtBSrc));
  Adder #(.width(32)) adder_1 (.a(multiplexer_1_out), .b(multiplexer_2_out), .out(adder_1_out));  // open: cin, cout
  Multiplexer #(.width(32), .enable("false")) multiplexer_3 (
    .in0(adder_1_out), .in1(Initial_Address), .out(multiplexer_3_out), .sel(Reset));
  Register #(.width(32), .Select("low")) register_1 (
    .D(multiplexer_3_out), .Q(PC), .clk(CLK), .cs(halt));  // open: en, clr, preset
  ROM #(.addrWidth(16), .dataWidth(32), .Select("high")) rom_1 (.addr(PC[17:2]), .data(IR));

  // Other names for the same wires on the sheet: Init_Addr[31:0] = Initial_Address

  // Notes on the sheet:
  //   Imm: pull=down
  //   BusA: pull=down
  //   NxtASrc: pull=down
  //   NxtBSrc: pull=down
  //   输入信号
  //   请勿修改引脚名称、电路名称及电路封装外观
  //   指令存储器256KB，数据位为32位，地址位为16位。PC寄存器数据宽度32位，片选信号高电平有效
  //   输出信号
  //   contents of rom_1 (hex, n*v repeats v):
  //   256*0 2083 8133 106213 406293 fff06313 4410663 106193 406393 806413 21b5b3 2058063 3a483 42503
  //   a4b5b3 458c63 a3a023 942023 c0006f 610133 fc9ff06f 4181b3 5383b3 540433 fc9ff06f 6f 0 0 413 9117
  //   ffc10113 94000ef 50463 8067 ff010113 100513 112623 74000ef ff010113 812423 912223 15c00413 1212023
  //   112623 c400493 9840913 442783 42703 4a503 440413 e787b3 40f50533 153513 f42223 448493 fa5ff0ef
  //   fd241ce3 100513 f99ff0ef c12083 812403 412483 12903 513 1010113 8067 1ea02e23 6f ff010113 b800513
  //   112623 f7dff0ef 1ea02e23 6f 0 1 1 2 3 5 8 d 15 22 37 59 90 e9 179 262 3db 63d a18 1055 1a6d 2ac2
  //   452f 6ff1 b520 12511 1da31 2ff42 4d973 7d8b5 cb228 148add 213d05 35c7e2 5704e7 8cccc9 e3d1b0 1709e79
  //   2547029 3c50ea2 6197ecb 1 1 deadbeef 395*0 413 9117 ffc10113 ec000ef 50463 8067 ff010113 100513
  //   112623 cc000ef ff010113 19400813 112623 812423 912223 1212023 100793 f82223 f82023 880593 7c80313
  //   100713 19800513 100893 50493 50793 100693 80006f 7a703 d70633 c7a023 478793 70693 feb796e3 117a023
  //   478593 658663 482703 fc9ff06f 11400413 7c40913 100793 c0006f 4a783 448493 42503 440413 40f50533
  //   153513 f4dff0ef fe8912e3 100513 f41ff0ef c12083 812403 412483 12903 513 1010113 8067 18a02823 6f
  //   ff010113 11000513 112623 f25ff0ef 18a02823 6f 0 1 1e 1b3 fdc 6b0d 22caa 90f6f 1f1058 594efd da4f4e
  //   1ca7357 3418be4 527c829 72363ea 8aaf953 93ee7d0 8aaf953 72363ea 527c829 3418be4 1ca7357 da4f4e
  //   594efd 1f1058 90f6f 22caa 6b0d fdc 1b3 1e 1 2 3 4 5 6 7 8 9 a b c d e f 10 11 12 13 14 15 16 17 18
  //   19 1a 1b 1c 1d 1e 1f deadbeef deadbeef 444*0 413 9117 ffc10113 39c000ef 50463 8067 ff010113 100513
  //   112623 380000ef 259693 d506b3 50893 6a803 60513 6c5dc63 261793 f887b3 7a783 fff50613 261613 c88633
  //   140006f fff50513 472783 6b50863 70613 ffc60713 fef846e3 259693 d886b3 251313 f6a023 688633 4a5de63
  //   68713 c0006f 158593 2a58463 72783 70693 470713 fef856e3 f62023 f8a5cee3 58513 106a023 8067 6886b3
  //   6a783 f62023 106a023 8067 251693 d886b3 f6a023 fe9ff06f 58513 fe1ff06f 1ec5da63 fa010113 4812c23
  //   5612023 3812c23 4112e23 4912a23 5212823 5312623 5412423 5512223 3712e23 3912a23 3a12823 3b12623
  //   58c13 60b13 50413 b0613 c0593 40513 ee9ff0ef a12223 fff50c93 159c5663 c8613 c0593 40513 ecdff0ef
  //   a12423 fff50d13 13ac5263 d0613 c0593 40513 eb1ff0ef a12623 fff50d93 fbc5e63 d8613 c0593 40513
  //   e95ff0ef a12823 fff50993 d3c5a63 98613 c0593 40513 e79ff0ef fff50913 50493 b2c5863 90613 c0593 40513
  //   e5dff0ef fff50b93 50a13 97c5663 b8613 c0593 40513 e41ff0ef a12a23 fff50a93 75c5263 a8613 c0593 40513
  //   e25ff0ef fff50693 50713 4dc5063 68613 c0593 40513 e12e23 d12c23 e01ff0ef 50813 c0593 fff50613 40513
  //   180c13 eadff0ef 1812683 1c12703 fcdc44e3 170c13 fb5c42e3 1412783 178c13 f77c4ee3 1a0c13 f52c4ce3
  //   148c13 f33c4ae3 1012783 178c13 f1bc46e3 c12783 178c13 efac42e3 812783 178c13 eb9c4ee3 412783 178c13
  //   e96c4ae3 5c12083 5812403 5412483 5012903 4c12983 4812a03 4412a83 4012b03 3c12b83 3812c03 3412c83
  //   3012d03 2c12d83 6010113 8067 8067 fe010113 1412423 1300613 593 3c000513 812c23 912a23 1212823
  //   1312623 112e23 3c000493 dddff0ef 3c000913 413 1400993 92503 490913 40850533 153513 140413 cddff0ef
  //   ff3414e3 100513 cd1ff0ef 1300613 593 3c000513 d9dff0ef 413 1400913 4a503 448493 40850533 153513
  //   140413 ca1ff0ef ff2414e3 100513 c95ff0ef 1c12083 1812403 1412483 1012903 c12983 812a03 513 2010113
  //   8067 6f ff010113 3bc00513 112623 f31ff0ef 6f 0 2 c e 6 d f 10 a 0 12 b 13 9 1 7 5 4 3 8 11 deadbeef
  //   deadbeef 63658*0 413 9117 ffc10113 39c000ef 50463 8067 ff010113 100513 112623 380000ef 259693 d506b3
  //   50893 6a803 60513 6c5dc63 261793 f887b3 7a783 fff50613 261613 c88633 140006f fff50513 472783 6b50863
  //   70613 ffc60713 fef846e3 259693 d886b3 251313 f6a023 688633 4a5de63 68713 c0006f 158593 2a58463 72783
  //   70693 470713 fef856e3 f62023 f8a5cee3 58513 106a023 8067 6886b3 6a783 f62023 106a023 8067 251693
  //   d886b3 f6a023 fe9ff06f 58513 fe1ff06f 1ec5da63 fa010113 4812c23 5612023 3812c23 4112e23 4912a23
  //   5212823 5312623 5412423 5512223 3712e23 3912a23 3a12823 3b12623 58c13 60b13 50413 b0613 c0593 40513
  //   ee9ff0ef a12223 fff50c93 159c5663 c8613 c0593 40513 ecdff0ef a12423 fff50d13 13a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
endmodule

module \控制器  (
  input  [6:0] opcode,
  input  [2:0] funct3,
  input  [6:0] funct7,
  output [2:0] ExtOp,
  output RegWr,
  output [2:0] Branch,
  output ALUASrc,
  output [1:0] ALUBSrc,
  output [3:0] ALUctr,
  output MemtoReg,
  output [2:0] MemOp,
  output MemWr,
  output Halt
);

  wire and_1_out, and_2_out, and_3_out, and_4_out, and_5_out, and_6_out, and_7_out, and_8_out, and_9_out,
       and_10_out, and_11_out, and_12_out, and_13_out, and_14_out, and_15_out, and_16_out, and_17_out,
       and_18_out, and_19_out, and_20_out, and_21_out, and_22_out, and_23_out, and_24_out, and_25_out,
       and_26_out, and_27_out, and_28_out, and_29_out, and_30_out, and_31_out, and_32_out, and_33_out,
       and_34_out, and_35_out, and_36_out, and_37_out, comparator_6_eq, comparator_7_eq, comparator_8_eq,
       comparator_9_eq, comparator_10_eq, comparator_11_eq, comparator_12_eq, comparator_13_eq,
       comparator_14_eq, comparator_14_gt, comparator_15_eq, comparator_15_gt, comparator_16_eq,
       comparator_17_eq, comparator_18_eq, comparator_19_eq, comparator_20_eq, comparator_21_eq,
       comparator_22_eq, comparator_23_eq, comparator_29_eq, comparator_30_eq, comparator_31_eq,
       comparator_32_eq, comparator_33_eq, comparator_34_eq, comparator_35_eq, comparator_36_eq,
       comparator_37_eq, comparator_38_eq, comparator_39_eq, comparator_42_eq, comparator_43_eq,
       comparator_44_eq, comparator_45_eq, comparator_46_eq, comparator_47_eq, comparator_48_eq, I_Arith,
       J_Jalr, or_1_out, or_2_out, or_7_out, or_8_out, or_9_out, or_13_out, or_14_out, or_15_out, or_16_out,
       or_22_out, or_23_out, or_24_out, or_25_out, or_27_out, R_Arith, U_auipc, U_lui;

  Comparator #(.width(7), .mode("unsigned")) comparator_1 (.a(opcode), .b(7'b0100011), .eq(MemWr));  // open: gt, lt
  Comparator #(.width(7), .mode("unsigned")) comparator_2 (.a(opcode), .b(7'b0110111), .eq(U_lui));  // open: gt, lt
  Comparator #(.width(7), .mode("unsigned")) comparator_3 (.a(opcode), .b(7'b0000011), .eq(MemtoReg));  // open: gt, lt
  Comparator #(.width(7), .mode("unsigned")) comparator_4 (.a(opcode), .b(7'b0010111), .eq(U_auipc));  // open: gt, lt
  Comparator #(.width(7), .mode("unsigned")) comparator_5 (.a(opcode), .b(7'b1100011), .eq(Branch[2]));  // open: gt, lt
  Comparator #(.width(3), .mode("unsigned")) comparator_6 (
    .a(funct3), .b(3'b001), .eq(comparator_6_eq));  // open: gt, lt
  Comparator #(.width(1), .mode("unsigned")) comparator_7 (
    .a(funct7[5]), .b(1'b0), .eq(comparator_7_eq));  // open: gt, lt
  Comparator #(.width(3), .mode("unsigned")) comparator_8 (
    .a(funct3), .b(3'b101), .eq(comparator_8_eq));  // open: gt, lt
  Comparator #(.width(1), .mode("unsigned")) comparator_9 (
    .a(funct7[5]), .b(1'b1), .eq(comparator_9_eq));  // open: gt, lt
  Comparator #(.width(3), .mode("unsigned")) comparator_10 (
    .a(funct3), .b(3'b001), .eq(comparator_10_eq));  // open: gt, lt
  Comparator #(.width(1), .mode("unsigned")) comparator_11 (
    .a(funct7[5]), .b(1'b0), .eq(comparator_11_eq));  // open: gt, lt
  Comparator #(.width(1), .mode("unsigned")) comparator_12 (
    .a(funct7[5]), .b(1'b1), .eq(comparator_12_eq));  // open: gt, lt
  Comparator #(.width(3), .mode("unsigned")) comparator_13 (
    .a(funct3), .b(3'b011), .eq(comparator_13_eq));  // open: gt, lt
  Comparator #(.width(3), .mode("unsigned")) comparator_14 (
    .a(funct3), .b(3'b101), .gt(comparator_14_gt), .eq(comparator_14_eq));  // open: lt
  Comparator #(.width(3), .mode("unsigned")) comparator_15 (
    .a(funct3), .b(3'b111), .gt(comparator_15_gt), .eq(comparator_15_eq));  // open: lt
  Comparator #(.width(3), .mode("unsigned")) comparator_16 (
    .a(funct3), .b(3'b001), .eq(comparator_16_eq));  // open: gt, lt
  or or_1 (or_1_out, comparator_16_eq, comparator_17_eq, comparator_18_eq);
  Comparator #(.width(3), .mode("unsigned")) comparator_17 (
    .a(funct3), .b(3'b101), .eq(comparator_17_eq));  // open: gt, lt
  Comparator #(.width(3), .mode("unsigned")) comparator_18 (
    .a(funct3), .b(3'b111), .eq(comparator_18_eq));  // open: gt, lt
  Comparator #(.width(3), .mode("unsigned")) comparator_19 (
    .a(funct3), .b(3'b100), .eq(comparator_19_eq));  // open: gt, lt
  or or_2 (or_2_out, comparator_19_eq, comparator_17_eq, comparator_18_eq, comparator_20_eq);
  Comparator #(.width(3), .mode("unsigned")) comparator_20 (
    .a(funct3), .b(3'b110), .eq(comparator_20_eq));  // open: gt, lt
  Comparator #(.width(3), .mode("unsigned")) comparator_21 (
    .a(funct3), .b(3'b110), .eq(comparator_21_eq));  // open: gt, lt
  Comparator #(.width(3), .mode("unsigned")) comparator_22 (
    .a(funct3), .b(3'b011), .eq(comparator_22_eq));  // open: gt, lt
  Comparator #(.width(3), .mode("unsigned")) comparator_23 (
    .a(funct3), .b(3'b111), .eq(comparator_23_eq));  // open: gt, lt
  and and_1 (and_1_out, comparator_6_eq, comparator_7_eq);
  and and_2 (and_2_out, comparator_7_eq, comparator_8_eq);
  and and_3 (and_3_out, comparator_8_eq, comparator_9_eq);
  or or_3 (RegWr, U_auipc, I_Arith, R_Arith, U_lui, MemtoReg, J_Jalr, ExtOp[2]);
  or or_4 (ALUASrc, U_auipc, J_Jalr, ExtOp[2]);
  or or_5 (ALUBSrc[0], J_Jalr, ExtOp[2]);
  or or_6 (ALUBSrc[1], MemWr, U_lui, U_auipc, I_Arith, MemtoReg);
  or or_7 (or_7_out, comparator_21_eq, comparator_23_eq);
  and and_4 (and_4_out, comparator_10_eq, comparator_11_eq);
  and and_5 (and_5_out, comparator_11_eq, comparator_13_eq);
  and and_6 (and_6_out, comparator_11_eq, comparator_14_eq);
  and and_7 (and_7_out, comparator_12_eq, comparator_14_eq);
  and and_8 (and_8_out, comparator_15_eq, comparator_11_eq);
  Comparator #(.width(7), .mode("unsigned")) comparator_24 (.a(opcode), .b(7'b0010011), .eq(I_Arith));  // open: gt, lt
  Comparator #(.width(7), .mode("unsigned")) comparator_25 (.a(opcode), .b(7'b1100111), .eq(J_Jalr));  // open: gt, lt
  and and_9 (and_9_out, or_1_out, Branch[2]);
  and and_10 (and_10_out, or_2_out, Branch[2]);
  or or_8 (or_8_out, comparator_22_eq, comparator_23_eq, and_1_out, and_2_out, and_3_out);
  or or_9 (or_9_out, and_4_out, and_5_out, and_6_out, and_7_out, and_8_out);
  or or_10 (Branch[0], ExtOp[2], and_9_out);
  or or_11 (Branch[1], J_Jalr, and_10_out);
  and and_11 (and_11_out, or_7_out, Branch[2]);
  and and_12 (and_12_out, or_8_out, I_Arith);
  and and_13 (and_13_out, or_9_out, R_Arith);
  Comparator #(.width(7), .mode("unsigned")) comparator_26 (.a(opcode), .b(7'b0110011), .eq(R_Arith));  // open: gt, lt
  Comparator #(.width(7), .mode("unsigned")) comparator_27 (.a(opcode), .b(7'b1101111), .eq(ExtOp[2]));  // open: gt, lt
  Comparator #(.width(7), .mode("unsigned")) comparator_28 (.a(opcode), .b(7'b1110011), .eq(Halt));  // open: gt, lt
  Comparator #(.width(3), .mode("unsigned")) comparator_29 (
    .a(funct3), .b(3'b100), .eq(comparator_29_eq));  // open: gt, lt
  Comparator #(.width(3), .mode("unsigned")) comparator_30 (
    .a(funct3), .b(3'b000), .eq(comparator_30_eq));  // open: gt, lt
  Comparator #(.width(3), .mode("unsigned")) comparator_31 (
    .a(funct3), .b(3'b001), .eq(comparator_31_eq));  // open: gt, lt
  Comparator #(.width(3), .mode("unsigned")) comparator_32 (
    .a(funct3), .b(3'b101), .eq(comparator_32_eq));  // open: gt, lt
  or or_12 (ALUctr[0], and_12_out, U_lui, and_13_out, and_11_out);
  or or_13 (or_13_out, comparator_29_eq, comparator_30_eq);
  or or_14 (or_14_out, comparator_31_eq, comparator_32_eq);
  or or_15 (or_15_out, comparator_30_eq, comparator_31_eq);
  or or_16 (or_16_out, comparator_30_eq, comparator_31_eq);
  and and_14 (and_14_out, or_13_out, MemtoReg);
  or or_17 (MemOp[0], and_14_out, and_15_out);
  and and_15 (and_15_out, comparator_30_eq, MemWr);
  and and_16 (and_16_out, or_14_out, MemtoReg);
  or or_18 (MemOp[1], and_16_out, and_17_out);
  and and_17 (and_17_out, comparator_31_eq, MemWr);
  and and_18 (and_18_out, or_15_out, MemtoReg);
  or or_19 (MemOp[2], and_18_out, and_19_out);
  and and_19 (and_19_out, or_16_out, MemWr);
  Comparator #(.width(1), .mode("unsigned")) comparator_33 (
    .a(funct7[5]), .b(1'b0), .eq(comparator_33_eq));  // open: gt, lt
  Comparator #(.width(3), .mode("unsigned")) comparator_34 (
    .a(funct3), .b(3'b010), .eq(comparator_34_eq));  // open: gt, lt
  Comparator #(.width(3), .mode("unsigned")) comparator_35 (
    .a(funct3), .b(3'b011), .eq(comparator_35_eq));  // open: gt, lt
  Comparator #(.width(3), .mode("unsigned")) comparator_36 (
    .a(funct3), .b(3'b110), .eq(comparator_36_eq));  // open: gt, lt
  Comparator #(.width(3), .mode("unsigned")) comparator_37 (
    .a(funct3), .b(3'b111), .eq(comparator_37_eq));  // open: gt, lt
  or or_20 (ExtOp[1], Branch[2], MemWr);
  or or_21 (ExtOp[0], U_lui, U_auipc, Branch[2]);
  and and_20 (and_20_out, comparator_34_eq, comparator_33_eq);
  and and_21 (and_21_out, comparator_35_eq, comparator_33_eq);
  and and_22 (and_22_out, comparator_36_eq, comparator_33_eq);
  and and_23 (and_23_out, comparator_37_eq, comparator_33_eq);
  Comparator #(.width(1), .mode("unsigned")) comparator_38 (
    .a(funct7[5]), .b(1'b1), .eq(comparator_38_eq));  // open: gt, lt
  Comparator #(.width(1), .mode("unsigned")) comparator_39 (
    .a(funct7[5]), .b(1'b0), .eq(comparator_39_eq));  // open: gt, lt
  Comparator #(.width(3), .mode("unsigned")) comparator_40 (.a(funct3), .b(3'b010));  // open: gt, eq, lt
  Comparator #(.width(3), .mode("unsigned")) comparator_41 (.a(funct3), .b(3'b011));  // open: gt, eq, lt
  Comparator #(.width(3), .mode("unsigned")) comparator_42 (
    .a(funct3), .b(3'b100), .eq(comparator_42_eq));  // open: gt, lt
  Comparator #(.width(3), .mode("unsigned")) comparator_43 (
    .a(funct3), .b(3'b110), .eq(comparator_43_eq));  // open: gt, lt
  Comparator #(.width(3), .mode("unsigned")) comparator_44 (
    .a(funct3), .b(3'b111), .eq(comparator_44_eq));  // open: gt, lt
  Comparator #(.width(3), .mode("unsigned")) comparator_45 (
    .a(funct3), .b(3'b101), .eq(comparator_45_eq));  // open: gt, lt
  or or_22 (or_22_out, comparator_34_eq, comparator_35_eq, comparator_36_eq, comparator_37_eq);
  or or_23 (or_23_out, and_20_out, and_21_out, and_22_out, and_23_out);
  and and_24 (and_24_out, or_22_out, I_Arith);
  and and_25 (and_25_out, R_Arith, or_23_out);
  and and_26 (and_26_out, comparator_42_eq, comparator_39_eq);
  and and_27 (and_27_out, comparator_45_eq, comparator_39_eq);
  and and_28 (and_28_out, comparator_45_eq, comparator_38_eq);
  and and_29 (and_29_out, comparator_43_eq, comparator_39_eq);
  and and_30 (and_30_out, comparator_44_eq, comparator_39_eq);
  or or_24 (or_24_out, comparator_43_eq, comparator_42_eq, comparator_44_eq, comparator_45_eq);
  or or_25 (or_25_out, and_26_out, and_27_out, and_28_out, and_29_out, and_30_out);
  or or_26 (ALUctr[1], Branch[2], and_24_out, and_25_out, U_lui);
  Comparator #(.width(1), .mode("unsigned")) comparator_46 (
    .a(funct7[5]), .b(1'b1), .eq(comparator_46_eq));  // open: gt, lt
  Comparator #(.width(3), .mode("unsigned")) comparator_47 (
    .a(funct3), .b(3'b000), .eq(comparator_47_eq));  // open: gt, lt
  Comparator #(.width(3), .mode("unsigned")) comparator_48 (
    .a(funct3), .b(3'b101), .eq(comparator_48_eq));  // open: gt, lt
  and and_31 (and_31_out, or_24_out, I_Arith);
  and and_32 (and_32_out, or_25_out, R_Arith);
  and and_33 (and_33_out, comparator_47_eq, comparator_46_eq);
  and and_34 (and_34_out, comparator_48_eq, comparator_46_eq);
  or or_27 (or_27_out, and_33_out, and_34_out);
  or or_28 (ALUctr[2], U_lui, and_31_out, and_32_out);
  and and_35 (and_35_out, comparator_46_eq, comparator_48_eq);
  and and_36 (and_36_out, and_35_out, I_Arith);
  and and_37 (and_37_out, or_27_out, R_Arith);
  or or_29 (ALUctr[3], U_lui, and_36_out, and_37_out);

  // Other names for the same wires on the sheet: B_Instr = Branch[2]; J_Jal = ExtOp[2]; L_Load = MemtoReg;
  //   S_Instr = MemWr

  // Notes on the sheet:
  //   输入引脚
  //   请勿修改引脚名称、电路名称及电路封装外观
  //   提示：根据指令种类，把7位指令code用一位指令类型标志位来表示，再通过功能码来区分具体指令，生成控制信号。
  //   输出引脚
endmodule

module IDU (
  input  [31:0] IR,
  input  [31:0] BusW,
  input  [31:0] PC,
  input  [2:0] ExtOp,
  input  RegWr,
  input  ALUASrc,
  input  [1:0] ALUBSrc,
  input  CLK,
  output [31:0] DataA,
  output [31:0] DataB,
  output [31:0] BusA,
  output [31:0] BusB,
  output [6:0] OpCode,
  output [31:0] Imm,
  output [2:0] Funct3,
  output [6:0] Funct7
);

  \立即数扩展器  \u_立即数扩展器_1  (.Instr(IR), .Extop(ExtOp), .imm(Imm));
  RegFile regfile_1 (
    .R1_num(IR[19:15]), .R2_num(IR[24:20]), .Write_Reg_num(IR[11:7]), .Write_Enable(RegWr), .Clock(CLK),
    .Din(BusW), .Reg1Out(BusA), .Reg2Out(BusB));
  Multiplexer #(.width(32), .enable("false")) multiplexer_1 (.in0(BusA), .in1(PC), .out(DataA), .sel(ALUASrc));
  Multiplexer #(.select(2), .width(32), .enable("false")) multiplexer_2 (
    .in0(BusB), .in1(32'h4), .in2(Imm), .out(DataB), .sel(ALUBSrc));  // open: in3

  assign Funct3 = IR[14:12];
  assign Funct7 = IR[31:25];
  assign OpCode = IR[6:0];

  // Other names for the same wires on the sheet: op[6:0] = IR[6:0]

  // Notes on the sheet:
  //   ALUBSrc: pull=down
  //   ALUASrc: pull=down
  //   BusW: pull=down
  //   RegWr: pull=down
  //   PC: pull=down
  //   ExtOp: pull=down
  //   输入信号
  //   funct7 rs2 rs1 funct3 rd opcode
  //   为了后续实验中的引用，不要修改ALUASrc、ALUBSrc和EXtOP编码定义。
  //   请勿修改引脚名称、电路名称及电路封装外观
  //   输出信号
  //   修改寄存器堆电路设计，0号寄存器始终为0。
endmodule

module RegFile (
  input  [4:0] R1_num,
  input  [4:0] R2_num,
  input  [4:0] Write_Reg_num,
  input  [31:0] Din,
  input  Write_Enable,
  input  Clock,
  output [31:0] Reg1Out,
  output [31:0] Reg2Out
);

  wire and_1_out, and_2_out, and_3_out, and_4_out, and_5_out, and_6_out, and_7_out, and_8_out, and_9_out,
       and_10_out, and_11_out, and_12_out, and_13_out, and_14_out, and_15_out, and_16_out, and_17_out,
       and_18_out, and_19_out, and_20_out, and_21_out, and_22_out, and_23_out, and_24_out, and_25_out,
       and_26_out, and_27_out, and_28_out, and_29_out, and_30_out, and_31_out, and_32_out, decoder_1_out0,
       decoder_1_out1, decoder_1_out2, decoder_1_out3, decoder_1_out4, decoder_1_out5, decoder_1_out6,
       decoder_1_out7, decoder_1_out8, decoder_1_out9, decoder_1_out10, decoder_1_out11, decoder_1_out12,
       decoder_1_out13, decoder_1_out14, decoder_1_out15, decoder_1_out16, decoder_1_out17, decoder_1_out18,
       decoder_1_out19, decoder_1_out20, decoder_1_out21, decoder_1_out22, decoder_1_out23, decoder_1_out24,
       decoder_1_out25, decoder_1_out26, decoder_1_out27, decoder_1_out28, decoder_1_out29, decoder_1_out30,
       decoder_1_out31;
  wire [31:0] _0_q, _1_q, _2_q, _3_q, _4_q, _5_q, _6_q, _7_q, _8_q, _9_q, register_1_q, register_2_q,
       register_3_q, register_4_q, register_5_q, register_6_q, register_7_q, register_8_q, register_9_q,
       register_10_q, register_11_q, register_12_q, register_13_q, register_14_q, register_15_q,
       register_16_q, register_17_q, register_18_q, register_19_q, register_20_q, register_21_q,
       register_22_q;

  Decoder #(.select(5), .enable("false")) decoder_1 (
    .out0(decoder_1_out0), .out1(decoder_1_out1), .out2(decoder_1_out2), .out3(decoder_1_out3),
    .out4(decoder_1_out4), .out5(decoder_1_out5), .out6(decoder_1_out6), .out7(decoder_1_out7),
    .out8(decoder_1_out8), .out9(decoder_1_out9), .out10(decoder_1_out10), .out11(decoder_1_out11),
    .out12(decoder_1_out12), .out13(decoder_1_out13), .out14(decoder_1_out14), .out15(decoder_1_out15),
    .out16(decoder_1_out16), .out17(decoder_1_out17), .out18(decoder_1_out18), .out19(decoder_1_out19),
    .out20(decoder_1_out20), .out21(decoder_1_out21), .out22(decoder_1_out22), .out23(decoder_1_out23),
    .out24(decoder_1_out24), .out25(decoder_1_out25), .out26(decoder_1_out26), .out27(decoder_1_out27),
    .out28(decoder_1_out28), .out29(decoder_1_out29), .out30(decoder_1_out30), .out31(decoder_1_out31),
    .sel(Write_Reg_num));
  and and_1 (and_1_out, Write_Enable, decoder_1_out0);
  and and_2 (and_2_out, Write_Enable, decoder_1_out1);
  and and_3 (and_3_out, Write_Enable, decoder_1_out2);
  and and_4 (and_4_out, Write_Enable, decoder_1_out3);
  and and_5 (and_5_out, Write_Enable, decoder_1_out4);
  and and_6 (and_6_out, Write_Enable, decoder_1_out5);
  and and_7 (and_7_out, Write_Enable, decoder_1_out6);
  and and_8 (and_8_out, Write_Enable, decoder_1_out7);
  and and_9 (and_9_out, Write_Enable, decoder_1_out8);
  and and_10 (and_10_out, Write_Enable, decoder_1_out9);
  and and_11 (and_11_out, Write_Enable, decoder_1_out10);
  and and_12 (and_12_out, Write_Enable, decoder_1_out11);
  and and_13 (and_13_out, Write_Enable, decoder_1_out12);
  and and_14 (and_14_out, Write_Enable, decoder_1_out13);
  and and_15 (and_15_out, Write_Enable, decoder_1_out14);
  and and_16 (and_16_out, Write_Enable, decoder_1_out15);
  and and_17 (and_17_out, Write_Enable, decoder_1_out16);
  and and_18 (and_18_out, Write_Enable, decoder_1_out17);
  and and_19 (and_19_out, Write_Enable, decoder_1_out18);
  and and_20 (and_20_out, Write_Enable, decoder_1_out19);
  and and_21 (and_21_out, Write_Enable, decoder_1_out20);
  and and_22 (and_22_out, Write_Enable, decoder_1_out21);
  and and_23 (and_23_out, Write_Enable, decoder_1_out22);
  and and_24 (and_24_out, Write_Enable, decoder_1_out23);
  and and_25 (and_25_out, Write_Enable, decoder_1_out24);
  and and_26 (and_26_out, Write_Enable, decoder_1_out25);
  and and_27 (and_27_out, Write_Enable, decoder_1_out26);
  and and_28 (and_28_out, Write_Enable, decoder_1_out27);
  and and_29 (and_29_out, Write_Enable, decoder_1_out28);
  and and_30 (and_30_out, Write_Enable, decoder_1_out29);
  and and_31 (and_31_out, Write_Enable, decoder_1_out30);
  and and_32 (and_32_out, Write_Enable, decoder_1_out31);
  Register #(.width(32), .Select("low")) _0 (.en(and_1_out), .Q(_0_q), .clk(Clock));  // open: D, clr
  Register #(.width(32), .Select("low")) _1 (.D(Din), .en(and_2_out), .Q(_1_q), .clk(Clock));  // open: clr
  Register #(.width(32), .Select("low")) _2 (.D(Din), .en(and_3_out), .Q(_2_q), .clk(Clock));  // open: clr
  Register #(.width(32), .Select("low")) _3 (.D(Din), .en(and_4_out), .Q(_3_q), .clk(Clock));  // open: clr
  Register #(.width(32), .Select("low")) _4 (.D(Din), .en(and_5_out), .Q(_4_q), .clk(Clock));  // open: clr
  Register #(.width(32), .Select("low")) _5 (.D(Din), .en(and_6_out), .Q(_5_q), .clk(Clock));  // open: clr
  Register #(.width(32), .Select("low")) _6 (.D(Din), .en(and_7_out), .Q(_6_q), .clk(Clock));  // open: clr
  Register #(.width(32), .Select("low")) _7 (.D(Din), .en(and_8_out), .Q(_7_q), .clk(Clock));  // open: clr
  Register #(.width(32), .Select("low")) _8 (.D(Din), .en(and_9_out), .Q(_8_q), .clk(Clock));  // open: clr
  Register #(.width(32), .Select("low")) _9 (.D(Din), .en(and_10_out), .Q(_9_q), .clk(Clock));  // open: clr
  Register #(.width(32), .Select("low")) register_1 (
    .D(Din), .en(and_11_out), .Q(register_1_q), .clk(Clock));  // open: clr
  Register #(.width(32), .Select("low")) register_2 (
    .D(Din), .en(and_12_out), .Q(register_2_q), .clk(Clock));  // open: clr
  Register #(.width(32), .Select("low")) register_3 (
    .D(Din), .en(and_13_out), .Q(register_3_q), .clk(Clock));  // open: clr
  Register #(.width(32), .Select("low")) register_4 (
    .D(Din), .en(and_14_out), .Q(register_4_q), .clk(Clock));  // open: clr
  Register #(.width(32), .Select("low")) register_5 (
    .D(Din), .en(and_15_out), .Q(register_5_q), .clk(Clock));  // open: clr
  Register #(.width(32), .Select("low")) register_6 (
    .D(Din), .en(and_16_out), .Q(register_6_q), .clk(Clock));  // open: clr
  Register #(.width(32), .Select("low")) register_7 (
    .D(Din), .en(and_17_out), .Q(register_7_q), .clk(Clock));  // open: clr
  Register #(.width(32), .Select("low")) register_8 (
    .D(Din), .en(and_18_out), .Q(register_8_q), .clk(Clock));  // open: clr
  Register #(.width(32), .Select("low")) register_9 (
    .D(Din), .en(and_19_out), .Q(register_9_q), .clk(Clock));  // open: clr
  Register #(.width(32), .Select("low")) register_10 (
    .D(Din), .en(and_20_out), .Q(register_10_q), .clk(Clock));  // open: clr
  Register #(.width(32), .Select("low")) register_11 (
    .D(Din), .en(and_21_out), .Q(register_11_q), .clk(Clock));  // open: clr
  Register #(.width(32), .Select("low")) register_12 (
    .D(Din), .en(and_22_out), .Q(register_12_q), .clk(Clock));  // open: clr
  Register #(.width(32), .Select("low")) register_13 (
    .D(Din), .en(and_23_out), .Q(register_13_q), .clk(Clock));  // open: clr
  Register #(.width(32), .Select("low")) register_14 (
    .D(Din), .en(and_24_out), .Q(register_14_q), .clk(Clock));  // open: clr
  Register #(.width(32), .Select("low")) register_15 (
    .D(Din), .en(and_25_out), .Q(register_15_q), .clk(Clock));  // open: clr
  Register #(.width(32), .Select("low")) register_16 (
    .D(Din), .en(and_26_out), .Q(register_16_q), .clk(Clock));  // open: clr
  Register #(.width(32), .Select("low")) register_17 (
    .D(Din), .en(and_27_out), .Q(register_17_q), .clk(Clock));  // open: clr
  Register #(.width(32), .Select("low")) register_18 (
    .D(Din), .en(and_28_out), .Q(register_18_q), .clk(Clock));  // open: clr
  Register #(.width(32), .Select("low")) register_19 (
    .D(Din), .en(and_29_out), .Q(register_19_q), .clk(Clock));  // open: clr
  Register #(.width(32), .Select("low")) register_20 (
    .D(Din), .en(and_30_out), .Q(register_20_q), .clk(Clock));  // open: clr
  Register #(.width(32), .Select("low")) register_21 (
    .D(Din), .en(and_31_out), .Q(register_21_q), .clk(Clock));  // open: clr
  Register #(.width(32), .Select("low")) register_22 (
    .D(Din), .en(and_32_out), .Q(register_22_q), .clk(Clock));  // open: clr
  Multiplexer #(.select(5), .width(32), .enable("false")) multiplexer_1 (
    .in0(_0_q), .in1(_1_q), .in2(_2_q), .in3(_3_q), .in4(_4_q), .in5(_5_q), .in6(_6_q), .in7(_7_q),
    .in8(_8_q), .in9(_9_q), .in10(register_1_q), .in11(register_2_q), .in12(register_3_q),
    .in13(register_4_q), .in14(register_5_q), .in15(register_6_q), .in16(register_7_q), .in17(register_8_q),
    .in18(register_9_q), .in19(register_10_q), .in20(register_11_q), .in21(register_12_q),
    .in22(register_13_q), .in23(register_14_q), .in24(register_15_q), .in25(register_16_q),
    .in26(register_17_q), .in27(register_18_q), .in28(register_19_q), .in29(register_20_q),
    .in30(register_21_q), .in31(register_22_q), .out(Reg1Out), .sel(R1_num));
  Multiplexer #(.select(5), .width(32), .enable("false")) multiplexer_2 (
    .in0(_0_q), .in1(_1_q), .in2(_2_q), .in3(_3_q), .in4(_4_q), .in5(_5_q), .in6(_6_q), .in7(_7_q),
    .in8(_8_q), .in9(_9_q), .in10(register_1_q), .in11(register_2_q), .in12(register_3_q),
    .in13(register_4_q), .in14(register_5_q), .in15(register_6_q), .in16(register_7_q), .in17(register_8_q),
    .in18(register_9_q), .in19(register_10_q), .in20(register_11_q), .in21(register_12_q),
    .in22(register_13_q), .in23(register_14_q), .in24(register_15_q), .in25(register_16_q),
    .in26(register_17_q), .in27(register_18_q), .in28(register_19_q), .in29(register_20_q),
    .in30(register_21_q), .in31(register_22_q), .out(Reg2Out), .sel(R2_num));

  // Other names for the same wires on the sheet: CLK = Clock; RA[4:0] = R1_num; RB[4:0] = R2_num; RDA[31:0] = Reg1Out;
  //   RDB[31:0] = Reg2Out; RW[4:0] = Write_Reg_num; WE = Write_Enable

  // Notes on the sheet:
  //   输入引脚
  //   请勿修改引脚名称、电路名称及电路封装外观
  //   提示：使用译码器、多路选择器和32位寄存器及逻辑门实现寄存器堆，禁止直接使用存储器组件。
  //   输出引脚
endmodule

module \立即数扩展器  (
  input  [31:0] Instr,
  input  [2:0] Extop,
  output [31:0] imm
);

  wire [11:0] bit_extender_1_out;
  wire [19:0] bit_extender_4_out;
  wire [31:0] bit_extender_2_out, bit_extender_3_out;

  assign bit_extender_1_out = {{11{Instr[31]}}, Instr[31]};  // Bit_Extender bit_extender_1
  assign bit_extender_2_out = {{20{Instr[31]}}, Instr[31:20]};  // Bit_Extender bit_extender_2
  assign bit_extender_3_out = {{20{Instr[31]}}, {Instr[31:25], Instr[11:7]}};  // Bit_Extender bit_extender_3
  assign bit_extender_4_out = {{19{Instr[31]}}, Instr[31]};  // Bit_Extender bit_extender_4
  Multiplexer #(.select(3), .width(32), .enable("false")) multiplexer_1 (
    .in0(bit_extender_2_out), .in1({Instr[31:12], {12{1'b0}}}), .in2(bit_extender_3_out),
    .in3({bit_extender_4_out, Instr[7], Instr[30:25], Instr[11:8], 1'b0}),
    .in4({bit_extender_1_out, Instr[19:12], Instr[20], Instr[30:21], 1'b0}), .out(imm), .sel(Extop));  // open: in5, in6, in7

  // Notes on the sheet:
  //   Instr: pull=down
  //   Extop: pull=down
  //   输入引脚
  //   输出引脚
endmodule

module DataRAM (
  input  CLK,
  input  CLR,
  input  WE,
  input  [2:0] MemOp,
  input  [17:0] Addr,
  input  [31:0] Din,
  output AlignErr,
  output [31:0] DataOut
);

  wire and_1_out, and_2_out, and_3_out, and_4_out, and_5_out, and_6_out, and_7_out, and_8_out, and_9_out,
       and_10_out, and_11_out, and_12_out, and_13_out, and_14_out, and_15_out, and_16_out, and_17_out,
       and_18_out, nand_1_out, SEL0, SEL1, SEL2, SEL3;
  wire [7:0] D1, D2, D3, D4, Dout0, Dout1, Dout2, Dout3, Ram0, Ram1, Ram2, Ram3;
  wire [31:0] bit_extender_1_out, bit_extender_2_out, bit_extender_3_out, bit_extender_4_out;

  RAM #(.addrWidth(16), .bus("separate"), .Select("high")) ram_1 (
    .addr(Addr[17:2]), .din(D1), .data(Ram3), .str(WE), .sel(SEL3), .clk(CLK), .ld(1'b1), .clr(CLR));
  and and_1 (and_1_out, ~MemOp[0], ~MemOp[1]);  // AND_Gate
  and and_2 (and_2_out, and_1_out, nand_1_out);
  nand nand_1 (nand_1_out, ~Addr[0], ~Addr[1]);  // NAND_Gate
  and and_3 (and_3_out, ~MemOp[0], MemOp[1], Addr[0], ~Addr[1]);  // AND_Gate
  and and_4 (and_4_out, MemOp[1], ~MemOp[0], Addr[0], Addr[1]);  // AND_Gate
  and and_5 (and_5_out, MemOp[1], MemOp[0]);
  and and_6 (and_6_out, ~MemOp[0], ~MemOp[1], MemOp[2], ~Addr[1], ~Addr[0]);  // AND_Gate
  and and_7 (and_7_out, ~Addr[1], ~Addr[0], ~MemOp[1], ~MemOp[0]);  // AND_Gate
  and and_8 (and_8_out, ~MemOp[1], MemOp[0], Addr[1], Addr[0]);  // AND_Gate
  and and_9 (and_9_out, MemOp[1], ~MemOp[0], Addr[1], ~Addr[0]);  // AND_Gate
  or or_1 (AlignErr, and_2_out, and_3_out, and_6_out, and_4_out, and_5_out);
  or or_2 (SEL3, and_7_out, and_8_out, and_9_out);
  RAM #(.addrWidth(16), .bus("separate"), .Select("high")) ram_2 (
    .addr(Addr[17:2]), .din(D2), .data(Ram2), .str(WE), .sel(SEL2), .clk(CLK), .ld(1'b1), .clr(CLR));
  RAM #(.addrWidth(16), .bus("separate"), .Select("high")) ram_3 (
    .addr(Addr[17:2]), .din(D3), .data(Ram1), .str(WE), .sel(SEL1), .clk(CLK), .ld(1'b1), .clr(CLR));
  and and_10 (and_10_out, ~MemOp[1], ~MemOp[0], ~Addr[1], ~Addr[0]);  // AND_Gate
  and and_11 (and_11_out, ~MemOp[1], MemOp[0], ~Addr[1], Addr[0]);  // AND_Gate
  and and_12 (and_12_out, MemOp[1], ~MemOp[0], ~Addr[1], ~Addr[0]);  // AND_Gate
  and and_13 (and_13_out, ~MemOp[1], ~MemOp[0], ~Addr[1], ~Addr[0]);  // AND_Gate
  and and_14 (and_14_out, ~MemOp[1], MemOp[0], ~Addr[1], ~Addr[0]);  // AND_Gate
  and and_15 (and_15_out, ~Addr[1], ~Addr[0], ~MemOp[1], ~MemOp[0]);  // AND_Gate
  and and_16 (and_16_out, MemOp[1], ~MemOp[0], Addr[1], ~Addr[0]);  // AND_Gate
  and and_17 (and_17_out, ~MemOp[1], MemOp[0], Addr[1], ~Addr[0]);  // AND_Gate
  or or_3 (SEL1, and_10_out, and_11_out, and_12_out);
  and and_18 (and_18_out, MemOp[1], ~MemOp[0], ~Addr[1], ~Addr[0]);  // AND_Gate
  RAM #(.addrWidth(16), .bus("separate"), .Select("high")) ram_4 (
    .addr(Addr[17:2]), .din(D4), .data(Ram0), .str(WE), .sel(SEL0), .clk(CLK), .ld(1'b1), .clr(CLR));
  or or_4 (SEL0, and_13_out, and_14_out, and_18_out);
  or or_5 (SEL2, and_15_out, and_16_out, and_17_out);
  assign bit_extender_1_out = {{24{1'b0}}, Dout0};  // Bit_Extender bit_extender_1
  assign bit_extender_2_out = {{16{1'b0}}, {Dout1, Dout0}};  // Bit_Extender bit_extender_2
  assign bit_extender_3_out = {{24{Dout0[7]}}, Dout0};  // Bit_Extender bit_extender_3
  assign bit_extender_4_out = {{16{Dout1[7]}}, {Dout1, Dout0}};  // Bit_Extender bit_extender_4
  Multiplexer #(.select(4), .width(8), .enable("false")) multiplexer_1 (
    .in0({8{1'b0}}), .in1({8{1'b0}}), .in2({8{1'b0}}), .in3({8{1'b0}}), .in4({8{1'b0}}), .in5({8{1'b0}}),
    .in6({8{1'b0}}), .in7({8{1'b0}}), .in8(Din[7:0]), .in9({8{1'b0}}), .in10({8{1'b0}}), .in11({8{1'b0}}),
    .in12(Din[15:8]), .in13({8{1'b0}}), .in14({8{1'b0}}), .in15(Din[31:24]), .out(D1),
    .sel({SEL3, SEL2, SEL1, SEL0}));
  Multiplexer #(.select(4), .width(8), .enable("false")) multiplexer_2 (
    .in0({8{1'b0}}), .in1({8{1'b0}}), .in2({8{1'b0}}), .in3({8{1'b0}}), .in4(Din[7:0]), .in5({8{1'b0}}),
    .in6({8{1'b0}}), .in7({8{1'b0}}), .in8({8{1'b0}}), .in9({8{1'b0}}), .in10({8{1'b0}}), .in11({8{1'b0}}),
    .in12(Din[7:0]), .in13({8{1'b0}}), .in14({8{1'b0}}), .in15(Din[23:16]), .out(D2),
    .sel({SEL3, SEL2, SEL1, SEL0}));
  Multiplexer #(.select(4), .width(8), .enable("false")) multiplexer_3 (
    .in0({8{1'b0}}), .in1({8{1'b0}}), .in2(Din[7:0]), .in3(Din[15:8]), .in4({8{1'b0}}), .in5({8{1'b0}}),
    .in6({8{1'b0}}), .in7({8{1'b0}}), .in8({8{1'b0}}), .in9({8{1'b0}}), .in10({8{1'b0}}), .in11({8{1'b0}}),
    .in12({8{1'b0}}), .in13({8{1'b0}}), .in14({8{1'b0}}), .in15(Din[15:8]), .out(D3),
    .sel({SEL3, SEL2, SEL1, SEL0}));
  Multiplexer #(.select(4), .width(8), .enable("false")) multiplexer_4 (
    .in0({8{1'b0}}), .in1(Din[7:0]), .in2({8{1'b0}}), .in3(Din[7:0]), .in4({8{1'b0}}), .in5({8{1'b0}}),
    .in6({8{1'b0}}), .in7({8{1'b0}}), .in8({8{1'b0}}), .in9({8{1'b0}}), .in10({8{1'b0}}), .in11({8{1'b0}}),
    .in12({8{1'b0}}), .in13({8{1'b0}}), .in14({8{1'b0}}), .in15(Din[7:0]), .out(D4),
    .sel({SEL3, SEL2, SEL1, SEL0}));
  Multiplexer #(.select(3), .width(32), .enable("false")) multiplexer_5 (
    .in0({Dout3, Dout2, Dout1, Dout0}), .in1(bit_extender_1_out), .in2(bit_extender_2_out),
    .in5(bit_extender_3_out), .in6(bit_extender_4_out), .out(DataOut), .sel(MemOp));  // open: in3, in4, in7
  Multiplexer #(.select(4), .width(8), .enable("false")) multiplexer_6 (
    .in1(Ram0), .in2(Ram1), .in3(Ram0), .in4(Ram2), .in8(Ram3), .in12(Ram2), .in15(Ram0), .out(Dout0),
    .sel({SEL3, SEL2, SEL1, SEL0}));  // open: in0, in5, in6, in7, in9, in10, in11, in13, in14
  Multiplexer #(.select(4), .width(8), .enable("false")) multiplexer_7 (
    .in3(Ram1), .in12(Ram3), .in15(Ram1), .out(Dout1), .sel({SEL3, SEL2, SEL1, SEL0}));  // open: in0, in1, in2, in4, in5, in6, in7, in8, in9, in10, in11, in13, in14
  Multiplexer #(.select(4), .width(8), .enable("false")) multiplexer_8 (
    .in15(Ram2), .out(Dout2), .sel({SEL3, SEL2, SEL1, SEL0}));  // open: in0, in1, in2, in3, in4, in5, in6, in7, in8, in9, in10, in11, in12, in13, in14
  Multiplexer #(.select(4), .width(8), .enable("false")) multiplexer_9 (
    .in15(Ram3), .out(Dout3), .sel({SEL3, SEL2, SEL1, SEL0}));  // open: in0, in1, in2, in3, in4, in5, in6, in7, in8, in9, in10, in11, in12, in13, in14

  // Other names for the same wires on the sheet: Dout[31:0] = DataOut

  // Notes on the sheet:
  //   输入引脚
  //   请勿修改引脚名称、电路名称及电路封装外观
  //   为了后续实验中的引用，不要修改MemOp的编码定义、引脚名称和在布局中的位置。
  //   32位数据存储器，按字节分4片存储，可按照字节、半字和字进行存储；读取字节或半字时，支持0扩展和符号位扩展。
  //   输出引脚
endmodule

module ALU (
  input  [3:0] ALUctr,
  input  [31:0] A,
  input  [31:0] B,
  output Zero,
  output [31:0] S
);

  wire adder32_1_cf, adder32_1_of, adder32_1_sf, aluctrl_1_alctr, aluctrl_1_sftctr, aluctrl_1_sigctr,
       aluctrl_1_subctr, multiplexer_2_out, xor_3_out;
  wire [2:0] aluctrl_1_opctr;
  wire [31:0] adder32_1_s, and_1_out, bit_extender_1_out, bit_extender_2_out, or_1_out, shifter32_1_dataout,
       xor_1_out, xor_2_out;

  assign bit_extender_1_out = {{31{aluctrl_1_subctr}}, aluctrl_1_subctr};  // Bit_Extender bit_extender_1
  assign and_1_out = A & B;  // AND_Gate and_1, 32 bits wide
  assign or_1_out = A | B;  // OR_Gate or_1, 32 bits wide
  assign xor_1_out = A ^ B;  // XOR_Gate xor_1, 32 bits wide
  Adder32 adder32_1 (
    .CF(adder32_1_cf), .OF(adder32_1_of), .SF(adder32_1_sf), .ZF(Zero), .X(A), .Y(xor_2_out),
    .Cin(aluctrl_1_subctr), .S(adder32_1_s));  // open: Cout
  assign xor_2_out = B ^ bit_extender_1_out;  // XOR_Gate xor_2, 32 bits wide
  Shifter32 shifter32_1 (
    .DataIn(A), .shamt(B[4:0]), .L_R(aluctrl_1_sftctr), .A_L(aluctrl_1_alctr), .DataOut(shifter32_1_dataout));
  xor xor_3 (xor_3_out, adder32_1_of, adder32_1_sf);
  Multiplexer #(.select(3), .width(32), .enable("false")) multiplexer_1 (
    .in0(adder32_1_s), .in1(and_1_out), .in2(or_1_out), .in3(xor_1_out), .in4(shifter32_1_dataout), .in5(B),
    .in6(bit_extender_2_out), .out(S), .sel(aluctrl_1_opctr));  // open: in7
  ALUctrl aluctrl_1 (
    .SUBctr(aluctrl_1_subctr), .SFTctr(aluctrl_1_sftctr), .SIGctr(aluctrl_1_sigctr), .ALctr(aluctrl_1_alctr),
    .OPctr(aluctrl_1_opctr), .ALUctr(ALUctr));
  // Probe on A
  // Probe on B
  // Probe on S
  Multiplexer #(.enable("false")) multiplexer_2 (
    .in0(adder32_1_cf), .in1(xor_3_out), .out(multiplexer_2_out), .sel(aluctrl_1_sigctr));
  assign bit_extender_2_out = {{31{1'b0}}, multiplexer_2_out};  // Bit_Extender bit_extender_2

  // Other names for the same wires on the sheet: Result[31:0] = S

  // Notes on the sheet:
  //   A: pull=down
  //   ALUctr: pull=down
  //   B: pull=down
  //   输入引脚
  //   请勿修改引脚名称、电路名称及电路封装外观
  //   提示：使用32位并行加法器子电路、桶形移位器、ALU控制子电路实现32位ALU
  //   功能说明:32位ALU，输入32位操作数A、B，4位控制信号ALUctr，输出32位结果Reseult和1位Zero标志位
  //   输出引脚
  //   操作数和结果
endmodule

module ALUctrl (
  input  [3:0] ALUctr,
  output SUBctr,
  output SFTctr,
  output SIGctr,
  output ALctr,
  output [2:0] OPctr
);

  wire and_1_out, and_2_out, and_3_out, and_4_out, and_5_out, and_6_out, and_7_out, and_8_out, and_9_out,
       and_10_out, and_11_out, and_12_out, and_13_out, and_14_out, and_15_out, and_16_out;

  and and_1 (and_1_out, ~ALUctr[3], ~ALUctr[2], ALUctr[1], ~ALUctr[0]);  // AND_Gate
  and and_2 (and_2_out, ~ALUctr[3], ~ALUctr[2], ALUctr[1], ALUctr[0]);  // AND_Gate
  and and_3 (and_3_out, ALUctr[3], ~ALUctr[2], ~ALUctr[1], ~ALUctr[0]);  // AND_Gate
  and and_4 (and_4_out, ~ALUctr[3], ALUctr[2], ~ALUctr[1], ~ALUctr[0]);  // AND_Gate
  and and_5 (and_5_out, ~ALUctr[3], ALUctr[2], ALUctr[1], ALUctr[0]);  // AND_Gate
  and and_6 (and_6_out, ALUctr[3], ALUctr[2], ALUctr[1], ALUctr[0]);
  and and_7 (and_7_out, ~ALUctr[3], ~ALUctr[2], ALUctr[1], ~ALUctr[0]);  // AND_Gate
  and and_8 (and_8_out, ~ALUctr[3], ~ALUctr[2], ALUctr[1], ALUctr[0]);  // AND_Gate
  and and_9 (and_9_out, ~ALUctr[3], ALUctr[2], ~ALUctr[1], ~ALUctr[0]);  // AND_Gate
  and and_10 (and_10_out, ~ALUctr[3], ALUctr[2], ALUctr[1], ~ALUctr[0]);  // AND_Gate
  and and_11 (and_11_out, ~ALUctr[3], ~ALUctr[2], ~ALUctr[1], ALUctr[0]);  // AND_Gate
  and and_12 (and_12_out, ~ALUctr[3], ~ALUctr[2], ALUctr[1], ~ALUctr[0]);  // AND_Gate
  and and_13 (and_13_out, ~ALUctr[3], ~ALUctr[2], ALUctr[1], ALUctr[0]);  // AND_Gate
  and and_14 (and_14_out, ~ALUctr[3], ALUctr[2], ~ALUctr[1], ALUctr[0]);  // AND_Gate
  and and_15 (and_15_out, ALUctr[3], ALUctr[2], ~ALUctr[1], ALUctr[0]);  // AND_Gate
  and and_16 (and_16_out, ALUctr[3], ALUctr[2], ALUctr[1], ALUctr[0]);
  or or_1 (SUBctr, and_1_out, and_2_out, and_3_out);
  and and_17 (SIGctr, ~ALUctr[3], ~ALUctr[2], ALUctr[1], ~ALUctr[0]);  // AND_Gate
  and and_18 (ALctr, ALUctr[3], ALUctr[2], ~ALUctr[1], ALUctr[0]);  // AND_Gate
  and and_19 (SFTctr, ~ALUctr[3], ~ALUctr[2], ~ALUctr[1], ALUctr[0]);  // AND_Gate
  or or_2 (OPctr[0], and_4_out, and_5_out, and_6_out);
  or or_3 (OPctr[1], and_7_out, and_8_out, and_9_out, and_10_out);
  or or_4 (OPctr[2], and_11_out, and_12_out, and_13_out, and_14_out, and_15_out, and_16_out);

  // Other names for the same wires on the sheet: LRctr = SFTctr

  // Notes on the sheet:
  //   输入引脚
  //   ALU操作控制信号生成部件
  //   输出引脚
endmodule

module Adder32 (
  input  Cin,
  input  [31:0] X,
  input  [31:0] Y,
  output CF,
  output Cout,
  output OF,
  output SF,
  output [31:0] S,
  output ZF
);

  wire adder16_2_c16, and_1_out, and_2_out, not_1_out, not_2_out, not_3_out;

  Adder16 adder16_1 (.X(X[31:16]), .Y(Y[31:16]), .C0(adder16_2_c16), .S(S[31:16]), .C16(Cout));  // open: Pg, Gg
  Adder16 adder16_2 (.X(X[15:0]), .Y(Y[15:0]), .C0(Cin), .S(S[15:0]), .C16(adder16_2_c16));  // open: Pg, Gg
  xor xor_1 (CF, Cout, Cin);
  not not_1 (not_1_out, X[31]);
  not not_2 (not_2_out, Y[31]);
  and and_1 (and_1_out, not_1_out, not_2_out, S[31]);
  not not_3 (not_3_out, S[31]);
  and and_2 (and_2_out, not_3_out, X[31], Y[31]);
  // Probe on X
  // Probe on Y
  // Probe on S
  Comparator #(.width(32), .mode("unsigned")) comparator_1 (.a(S), .b({32{1'b0}}), .eq(ZF));  // open: gt, lt
  or or_1 (OF, and_1_out, and_2_out);

  assign SF = S[31];

  // Notes on the sheet:
  //   X: pull=down
  //   Y: pull=down
  //   Cin: pull=down
  //   输入引脚区
  //   输出引脚区
  //   请勿修改引脚名称、电路名称及电路封装外观
  //   提示：使用16位并行加法器子电路实现32位快速加法器
  //   功能说明:32位Adder  S=X+Y，Cout为最高位进位位，Cin为进位输入， S为和，溢出OF、进位CF、零ZF、符号SF。
  //   +
  //   =
  //   无符号加法
endmodule

// 移位器
module Shifter32 (
  input  [4:0] shamt,
  input  L_R,
  input  A_L,
  input  [31:0] DataIn,
  output [31:0] DataOut
);

  wire [0:0] multiplexer_1_out;
  wire [1:0] multiplexer_6_out;
  wire [3:0] multiplexer_9_out;
  wire [7:0] multiplexer_15_out;
  wire [15:0] multiplexer_41_out;
  wire [31:0] multiplexer_3_out, multiplexer_8_out, multiplexer_13_out, multiplexer_23_out;
  wire [31:31] multiplexer_2_out, multiplexer_4_out, multiplexer_7_out, multiplexer_14_out,
       multiplexer_24_out;

  Multiplexer #(.enable("false")) multiplexer_1 (.in0(1'b0), .in1(DataIn[31]), .out(multiplexer_1_out[0]), .sel(A_L));
  Multiplexer #(.enable("false")) multiplexer_2 (.in0(1'b0), .in1(DataIn[31]), .out(multiplexer_2_out[31]), .sel(A_L));
  Multiplexer #(.select(2), .width(32), .enable("false")) multiplexer_3 (
    .in0(DataIn), .in1({multiplexer_2_out[31], DataIn[31:1]}), .in2(DataIn),
    .in3({DataIn[30:0], multiplexer_1_out[0]}), .out(multiplexer_3_out), .sel({L_R, shamt[0]}));
  Multiplexer #(.enable("false")) multiplexer_4 (
    .in0(1'b0), .in1(multiplexer_3_out[31]), .out(multiplexer_4_out[31]), .sel(A_L));
  Multiplexer #(.enable("false")) multiplexer_5 (
    .in0(1'b0), .in1(multiplexer_3_out[31]), .out(multiplexer_6_out[1]), .sel(A_L));
  Multiplexer #(.enable("false")) multiplexer_6 (
    .in0(1'b0), .in1(multiplexer_3_out[30]), .out(multiplexer_6_out[0]), .sel(A_L));
  Multiplexer #(.enable("false")) multiplexer_7 (
    .in0(1'b0), .in1(multiplexer_8_out[31]), .out(multiplexer_7_out[31]), .sel(A_L));
  Multiplexer #(.select(2), .width(32), .enable("false")) multiplexer_8 (
    .in0(multiplexer_3_out), .in1({{2{multiplexer_4_out[31]}}, multiplexer_3_out[31:2]}),
    .in2(multiplexer_3_out), .in3({multiplexer_3_out[29:0], multiplexer_6_out}), .out(multiplexer_8_out),
    .sel({L_R, shamt[1]}));
  Multiplexer #(.enable("false")) multiplexer_9 (
    .in0(1'b0), .in1(multiplexer_8_out[28]), .out(multiplexer_9_out[0]), .sel(A_L));
  Multiplexer #(.enable("false")) multiplexer_10 (
    .in0(1'b0), .in1(multiplexer_8_out[29]), .out(multiplexer_9_out[1]), .sel(A_L));
  Multiplexer #(.enable("false")) multiplexer_11 (
    .in0(1'b0), .in1(multiplexer_8_out[30]), .out(multiplexer_9_out[2]), .sel(A_L));
  Multiplexer #(.enable("false")) multiplexer_12 (
    .in0(1'b0), .in1(multiplexer_8_out[31]), .out(multiplexer_9_out[3]), .sel(A_L));
  Multiplexer #(.select(2), .width(32), .enable("false")) multiplexer_13 (
    .in0(multiplexer_8_out), .in1({{4{multiplexer_7_out[31]}}, multiplexer_8_out[31:4]}),
    .in2(multiplexer_8_out), .in3({multiplexer_8_out[27:0], multiplexer_9_out}), .out(multiplexer_13_out),
    .sel({L_R, shamt[2]}));
  Multiplexer #(.enable("false")) multiplexer_14 (
    .in0(1'b0), .in1(multiplexer_13_out[31]), .out(multiplexer_14_out[31]), .sel(A_L));
  Multiplexer #(.enable("false")) multiplexer_15 (
    .in0(1'b0), .in1(multiplexer_13_out[24]), .out(multiplexer_15_out[0]), .sel(A_L));
  Multiplexer #(.enable("false")) multiplexer_16 (
    .in0(1'b0), .in1(multiplexer_13_out[28]), .out(multiplexer_15_out[4]), .sel(A_L));
  Multiplexer #(.enable("false")) multiplexer_17 (
    .in0(1'b0), .in1(multiplexer_13_out[25]), .out(multiplexer_15_out[1]), .sel(A_L));
  Multiplexer #(.enable("false")) multiplexer_18 (
    .in0(1'b0), .in1(multiplexer_13_out[29]), .out(multiplexer_15_out[5]), .sel(A_L));
  Multiplexer #(.enable("false")) multiplexer_19 (
    .in0(1'b0), .in1(multiplexer_13_out[26]), .out(multiplexer_15_out[2]), .sel(A_L));
  Multiplexer #(.enable("false")) multiplexer_20 (
    .in0(1'b0), .in1(multiplexer_13_out[30]), .out(multiplexer_15_out[6]), .sel(A_L));
  Multiplexer #(.enable("false")) multiplexer_21 (
    .in0(1'b0), .in1(multiplexer_13_out[27]), .out(multiplexer_15_out[3]), .sel(A_L));
  Multiplexer #(.enable("false")) multiplexer_22 (
    .in0(1'b0), .in1(multiplexer_13_out[31]), .out(multiplexer_15_out[7]), .sel(A_L));
  Multiplexer #(.select(2), .width(32), .enable("false")) multiplexer_23 (
    .in0(multiplexer_13_out), .in1({{8{multiplexer_14_out[31]}}, multiplexer_13_out[31:8]}),
    .in2(multiplexer_13_out), .in3({multiplexer_13_out[23:0], multiplexer_15_out}), .out(multiplexer_23_out),
    .sel({L_R, shamt[3]}));
  Multiplexer #(.enable("false")) multiplexer_24 (
    .in0(1'b0), .in1(multiplexer_23_out[31]), .out(multiplexer_24_out[31]), .sel(A_L));
  Multiplexer #(.enable("false")) multiplexer_25 (
    .in0(1'b0), .in1(multiplexer_23_out[31]), .out(multiplexer_41_out[15]), .sel(A_L));
  Multiplexer #(.enable("false")) multiplexer_26 (
    .in0(1'b0), .in1(multiplexer_23_out[27]), .out(multiplexer_41_out[11]), .sel(A_L));
  Multiplexer #(.enable("false")) multiplexer_27 (
    .in0(1'b0), .in1(multiplexer_23_out[23]), .out(multiplexer_41_out[7]), .sel(A_L));
  Multiplexer #(.enable("false")) multiplexer_28 (
    .in0(1'b0), .in1(multiplexer_23_out[19]), .out(multiplexer_41_out[3]), .sel(A_L));
  Multiplexer #(.enable("false")) multiplexer_29 (
    .in0(1'b0), .in1(multiplexer_23_out[30]), .out(multiplexer_41_out[14]), .sel(A_L));
  Multiplexer #(.enable("false")) multiplexer_30 (
    .in0(1'b0), .in1(multiplexer_23_out[26]), .out(multiplexer_41_out[10]), .sel(A_L));
  Multiplexer #(.enable("false")) multiplexer_31 (
    .in0(1'b0), .in1(multiplexer_23_out[22]), .out(multiplexer_41_out[6]), .sel(A_L));
  Multiplexer #(.enable("false")) multiplexer_32 (
    .in0(1'b0), .in1(multiplexer_23_out[18]), .out(multiplexer_41_out[2]), .sel(A_L));
  Multiplexer #(.select(2), .width(32), .enable("false")) multiplexer_33 (
    .in0(multiplexer_23_out), .in1({{16{multiplexer_24_out[31]}}, multiplexer_23_out[31:16]}),
    .in2(multiplexer_23_out), .in3({multiplexer_23_out[15:0], multiplexer_41_out}), .out(DataOut),
    .sel({L_R, shamt[4]}));
  Multiplexer #(.enable("false")) multiplexer_34 (
    .in0(1'b0), .in1(multiplexer_23_out[29]), .out(multiplexer_41_out[13]), .sel(A_L));
  Multiplexer #(.enable("false")) multiplexer_35 (
    .in0(1'b0), .in1(multiplexer_23_out[25]), .out(multiplexer_41_out[9]), .sel(A_L));
  Multiplexer #(.enable("false")) multiplexer_36 (
    .in0(1'b0), .in1(multiplexer_23_out[21]), .out(multiplexer_41_out[5]), .sel(A_L));
  Multiplexer #(.enable("false")) multiplexer_37 (
    .in0(1'b0), .in1(multiplexer_23_out[17]), .out(multiplexer_41_out[1]), .sel(A_L));
  Multiplexer #(.enable("false")) multiplexer_38 (
    .in0(1'b0), .in1(multiplexer_23_out[28]), .out(multiplexer_41_out[12]), .sel(A_L));
  Multiplexer #(.enable("false")) multiplexer_39 (
    .in0(1'b0), .in1(multiplexer_23_out[24]), .out(multiplexer_41_out[8]), .sel(A_L));
  Multiplexer #(.enable("false")) multiplexer_40 (
    .in0(1'b0), .in1(multiplexer_23_out[20]), .out(multiplexer_41_out[4]), .sel(A_L));
  Multiplexer #(.enable("false")) multiplexer_41 (
    .in0(1'b0), .in1(multiplexer_23_out[16]), .out(multiplexer_41_out[0]), .sel(A_L));

  // Other names for the same wires on the sheet: Din[31:0] = DataIn; Left_Right = L_R; Arth_Logic = A_L;
  //   Dout[31:0] = DataOut

  // Notes on the sheet:
  //   上：右移，下：左移
  //   L/R,A/L: 00逻辑右移，01算术右移，10逻辑左移，11：循环左移
  //   输入引脚
  //   请勿修改引脚名称、电路名称及电路封装外观
  //   提示：使用多路选择器、逻辑门实现32位桶形移位器，禁止直接使用移位器组件。
  //   输出引脚
endmodule

module Adder16 (
  input  C0,
  input  [15:0] X,
  input  [15:0] Y,
  output C16,
  output Pg,
  output Gg,
  output [15:0] S
);

  wire cla4_1_gg, cla4_1_pg, cla4_2_gg, cla4_2_pg, cla4_3_gg, cla4_3_pg, cla4_4_gg, cla4_4_pg, clu4_1_c1,
       clu4_1_c2, clu4_1_c3;

  CLA4 cla4_1 (.X(X[15:12]), .F(S[15:12]), .Cout(C16), .Y(Y[15:12]), .Pg(cla4_1_pg), .Cin(clu4_1_c3), .Gg(cla4_1_gg));
  CLA4 cla4_2 (.X(X[11:8]), .F(S[11:8]), .Y(Y[11:8]), .Pg(cla4_2_pg), .Cin(clu4_1_c2), .Gg(cla4_2_gg));  // open: Cout
  CLU4 clu4_1 (
    .P0(cla4_4_pg), .P1(cla4_3_pg), .P2(cla4_2_pg), .P3(cla4_1_pg), .C1(clu4_1_c1), .C3(clu4_1_c3),
    .G0(cla4_4_gg), .G1(cla4_3_gg), .G2(cla4_2_gg), .G3(cla4_1_gg), .C2(clu4_1_c2), .C0(C0), .Pg(Pg), .Gg(Gg));  // open: C4
  CLA4 cla4_3 (.X(X[7:4]), .F(S[7:4]), .Y(Y[7:4]), .Pg(cla4_3_pg), .Cin(clu4_1_c1), .Gg(cla4_3_gg));  // open: Cout
  CLA4 cla4_4 (.X(X[3:0]), .F(S[3:0]), .Y(Y[3:0]), .Pg(cla4_4_pg), .Cin(C0), .Gg(cla4_4_gg));  // open: Cout
  // Probe on X
  // Probe on Y
  // Probe on S

  // Notes on the sheet:
  //   C0: pull=down
  //   Y: pull=down
  //   X: pull=down
  //   输入引脚区
  //   请勿修改引脚名称、电路名称及电路封装外观
  //   提示：使用4位先行进位加法器和CLU子电路实现16位并行加法器
  //   功能说明:16位Adder  S=X+Y，C16为最高位进位位，C0为进位输入， Pg、Gg为成组进位生成传递函数
  //   输出引脚区
  //   +
  //   =
  //   无符号加法
endmodule

module CLA4 (
  input  [3:0] X,
  input  [3:0] Y,
  input  Cin,
  output [3:0] F,
  output Cout,
  output Pg,
  output Gg
);

  wire clu4_1_c1, clu4_1_c2, clu4_1_c3, fa_1_g, fa_1_p, fa_2_g, fa_2_p, fa_3_g, fa_3_p, fa_4_g, fa_4_p;

  Hex_Digit_Display hex_digit_display_1 (.value(X));  // open: dp
  FA fa_1 (.A(X[3]), .F(F[3]), .B(Y[3]), .P(fa_1_p), .Cin(clu4_1_c3), .G(fa_1_g));
  Hex_Digit_Display hex_digit_display_2 (.value(Y));  // open: dp
  FA fa_2 (.A(X[2]), .F(F[2]), .B(Y[2]), .P(fa_2_p), .Cin(clu4_1_c2), .G(fa_2_g));
  FA fa_3 (.A(X[1]), .F(F[1]), .B(Y[1]), .P(fa_3_p), .Cin(clu4_1_c1), .G(fa_3_g));
  Hex_Digit_Display hex_digit_display_3 (.value(F));  // open: dp
  CLU4 clu4_1 (
    .P0(fa_4_p), .P1(fa_3_p), .P2(fa_2_p), .P3(fa_1_p), .C1(clu4_1_c1), .C3(clu4_1_c3), .G0(fa_4_g),
    .G1(fa_3_g), .G2(fa_2_g), .G3(fa_1_g), .C2(clu4_1_c2), .C4(Cout), .C0(Cin), .Pg(Pg), .Gg(Gg));
  FA fa_4 (.A(X[0]), .F(F[0]), .B(Y[0]), .P(fa_4_p), .Cin(Cin), .G(fa_4_g));

  // Other names for the same wires on the sheet: Z[3:0] = F

  // Notes on the sheet:
  //   +
  //   =
  //   输出
  //   输入
  //   请勿修改引脚名称、电路名称及电路封装外观
  //   提示：使用全加器和CLU子电路实现四位先行进位加法器CLA4
endmodule

module CLU4 (
  input  P0,
  input  P1,
  input  P2,
  input  P3,
  input  G0,
  input  G1,
  input  G2,
  input  G3,
  input  C0,
  output C1,
  output C3,
  output C2,
  output C4,
  output Pg,
  output Gg
);

  wire and_1_out, and_2_out, and_3_out, and_4_out, and_5_out, and_6_out, and_7_out, and_8_out, and_9_out,
       and_10_out, and_11_out, and_12_out, and_13_out;

  and and_1 (and_1_out, P3, P2, G1);
  and and_2 (and_2_out, P3, G2);
  or or_1 (C4, G3, and_2_out, and_1_out, and_4_out, and_3_out);
  and and_3 (and_3_out, P3, P2, P1, P0, C0);
  and and_4 (and_4_out, P3, P2, P1, G0);
  and and_5 (and_5_out, P2, G1);
  or or_2 (C3, G2, and_5_out, and_7_out, and_6_out);
  and and_6 (and_6_out, P2, P1, P0, C0);
  and and_7 (and_7_out, P2, P1, G0);
  and and_8 (and_8_out, P3, G2);
  or or_3 (Gg, G3, and_8_out, and_10_out, and_12_out);
  and and_9 (and_9_out, P1, G0);
  and and_10 (and_10_out, P3, P2, G1);
  or or_4 (C2, G1, and_9_out, and_11_out);
  and and_11 (and_11_out, P1, P0, C0);
  and and_12 (and_12_out, P3, P2, P1, G0);
  or or_5 (C1, G0, and_13_out);
  and and_13 (and_13_out, P0, C0);
  and and_14 (Pg, P0, P1, P2, P3);

  // Notes on the sheet:
  //   输入引脚
  //   请勿修改引脚名称、电路名称及电路封装外观
  //   提示：使用逻辑门电路实现4位四位先行进位部件CLU，Pg、Gg为成组进位生成传递函数
  //   输出引脚
endmodule

module FA (
  input  A,
  input  B,
  input  Cin,
  output F,
  output P,
  output G
);

  wire xor_1_out;

  or or_1 (P, A, B);
  and and_1 (G, A, B);
  xor xor_1 (xor_1_out, A, B);
  xor xor_2 (F, xor_1_out, Cin);

  // Notes on the sheet:
  //   输入引脚
  //   请勿修改引脚名称、电路名称及电路封装外观
  //   输出引脚
endmodule
